// Logisim project Abdullah Mahmood 1330639042 ALU Reg.circ as structural Verilog: 4 circuits, main circuit main
// CPU
module main (
  input  Cin,
  input  A_Invert,
  input  B_Invert,
  input  RegWrite,
  input  [3:0] RS_ReadReg01,
  input  [15:0] Input_A,
  input  [3:0] RT_ReadReg02,
  input  [3:0] RD_WriteReg,
  input  [15:0] Input_B,
  input  [15:0] Write_Data,
  input  [1:0] OpCode,
  output [15:0] ReadData01,
  output [15:0] Result,
  output [15:0] ReadData02
);

  wire Clock_out, n16bit_alus_1_overflow, n16bit_alus_1_zero_flag;

  Clock Clock (.out(Clock_out));
  RegisterFile registerfile_1 (
    .Write_Data_IN(Write_Data), .Data01(ReadData01), .Data02(ReadData02), .RD(RD_WriteReg),
    .RS(RS_ReadReg01), .RT(RT_ReadReg02), .Clock(Clock_out), .RegWrite(RegWrite));
  _16bit_ALUs u_16bit_alus_1 (
    .B_Invert(B_Invert), .A_Invert(A_Invert), .Zero_Flag(n16bit_alus_1_zero_flag), .Input_B(Input_B),
    .Input_A(Input_A), .Operation_Code(OpCode), .OverFlow(n16bit_alus_1_overflow), .Result(Result), .Cin(Cin));
  LED Zero_Flag (.in(n16bit_alus_1_zero_flag));
  LED OverFlow (.in(n16bit_alus_1_overflow));

  // Notes on the sheet:
  //   REG & ALU
  //   Abdullah Mahmood (133-0639-042)
  //   AbiMahmood
endmodule

// Register File
module RegisterFile (
  input  Clock,
  input  [15:0] Write_Data_IN,
  input  RegWrite,
  input  [3:0] RS,
  input  [3:0] RD,
  input  [3:0] RT,
  output [15:0] Data01,
  output [15:0] Data02
);

  wire and_1_out, and_2_out, and_3_out, and_4_out, and_5_out, and_6_out, and_7_out, and_8_out, and_9_out,
       and_10_out, and_11_out, and_12_out, and_13_out, and_14_out, and_15_out, and_16_out, decoder_1_out0,
       decoder_1_out1, decoder_1_out2, decoder_1_out3, decoder_1_out4, decoder_1_out5, decoder_1_out6,
       decoder_1_out7, decoder_1_out8, decoder_1_out9, decoder_1_out10, decoder_1_out11, decoder_1_out12,
       decoder_1_out13, decoder_1_out14, decoder_1_out15;
  wire [15:0] register_1_q, register_2_q, register_3_q, register_4_q, register_5_q, register_6_q,
       register_7_q, register_8_q, register_9_q, register_10_q, register_11_q, register_12_q, register_13_q,
       register_14_q, register_15_q, register_16_q;

  Decoder #(.select(4)) decoder_1 (
    .out0(decoder_1_out0), .out1(decoder_1_out1), .out2(decoder_1_out2), .out3(decoder_1_out3),
    .out4(decoder_1_out4), .out5(decoder_1_out5), .out6(decoder_1_out6), .out7(decoder_1_out7),
    .out8(decoder_1_out8), .out9(decoder_1_out9), .out10(decoder_1_out10), .out11(decoder_1_out11),
    .out12(decoder_1_out12), .out13(decoder_1_out13), .out14(decoder_1_out14), .out15(decoder_1_out15),
    .sel(RD));  // open: en
  and and_1 (and_1_out, RegWrite, decoder_1_out0);
  and and_2 (and_2_out, RegWrite, decoder_1_out1);
  and and_3 (and_3_out, RegWrite, decoder_1_out2);
  and and_4 (and_4_out, RegWrite, decoder_1_out3);
  and and_5 (and_5_out, RegWrite, decoder_1_out4);
  and and_6 (and_6_out, RegWrite, decoder_1_out5);
  and and_7 (and_7_out, RegWrite, decoder_1_out6);
  and and_8 (and_8_out, RegWrite, decoder_1_out7);
  and and_9 (and_9_out, RegWrite, decoder_1_out8);
  and and_10 (and_10_out, RegWrite, decoder_1_out9);
  and and_11 (and_11_out, RegWrite, decoder_1_out10);
  and and_12 (and_12_out, RegWrite, decoder_1_out11);
  and and_13 (and_13_out, RegWrite, decoder_1_out12);
  and and_14 (and_14_out, RegWrite, decoder_1_out13);
  and and_15 (and_15_out, RegWrite, decoder_1_out14);
  and and_16 (and_16_out, RegWrite, decoder_1_out15);
  Register #(.width(16)) register_1 (.D(Write_Data_IN), .en(and_1_out), .Q(register_1_q), .clk(Clock));  // open: clr
  Register #(.width(16)) register_2 (.D(Write_Data_IN), .en(and_2_out), .Q(register_2_q), .clk(Clock));  // open: clr
  Register #(.width(16)) register_3 (.D(Write_Data_IN), .en(and_3_out), .Q(register_3_q), .clk(Clock));  // open: clr
  Register #(.width(16)) register_4 (.D(Write_Data_IN), .en(and_4_out), .Q(register_4_q), .clk(Clock));  // open: clr
  Register #(.width(16)) register_5 (.D(Write_Data_IN), .en(and_5_out), .Q(register_5_q), .clk(Clock));  // open: clr
  Register #(.width(16)) register_6 (.D(Write_Data_IN), .en(and_6_out), .Q(register_6_q), .clk(Clock));  // open: clr
  Register #(.width(16)) register_7 (.D(Write_Data_IN), .en(and_7_out), .Q(register_7_q), .clk(Clock));  // open: clr
  Register #(.width(16)) register_8 (.D(Write_Data_IN), .en(and_8_out), .Q(register_8_q), .clk(Clock));  // open: clr
  Register #(.width(16)) register_9 (.D(Write_Data_IN), .en(and_9_out), .Q(register_9_q), .clk(Clock));  // open: clr
  Register #(.width(16)) register_10 (.D(Write_Data_IN), .en(and_10_out), .Q(register_10_q), .clk(Clock));  // open: clr
  Register #(.width(16)) register_11 (.D(Write_Data_IN), .en(and_11_out), .Q(register_11_q), .clk(Clock));  // open: clr
  Register #(.width(16)) register_12 (.D(Write_Data_IN), .en(and_12_out), .Q(register_12_q), .clk(Clock));  // open: clr
  Register #(.width(16)) register_13 (.D(Write_Data_IN), .en(and_13_out), .Q(register_13_q), .clk(Clock));  // open: clr
  Register #(.width(16)) register_14 (.D(Write_Data_IN), .en(and_14_out), .Q(register_14_q), .clk(Clock));  // open: clr
  Register #(.width(16)) register_15 (.D(Write_Data_IN), .en(and_15_out), .Q(register_15_q), .clk(Clock));  // open: clr
  Register #(.width(16)) register_16 (.D(Write_Data_IN), .en(and_16_out), .Q(register_16_q), .clk(Clock));  // open: clr
  Multiplexer #(.select(4), .width(16)) multiplexer_1 (
    .in0(register_1_q), .in1(register_2_q), .in2(register_3_q), .in3(register_4_q), .in4(register_5_q),
    .in5(register_6_q), .in6(register_7_q), .in7(register_8_q), .in8(register_9_q), .in9(register_10_q),
    .in10(register_11_q), .in11(register_12_q), .in12(register_13_q), .in13(register_14_q),
    .in14(register_15_q), .in15(register_16_q), .out(Data01), .sel(RS));  // open: en
  Multiplexer #(.select(4), .width(16)) multiplexer_2 (
    .in0(register_1_q), .in1(register_2_q), .in2(register_3_q), .in3(register_4_q), .in4(register_5_q),
    .in5(register_6_q), .in6(register_7_q), .in7(register_8_q), .in8(register_9_q), .in9(register_10_q),
    .in10(register_11_q), .in11(register_12_q), .in12(register_13_q), .in13(register_14_q),
    .in14(register_15_q), .in15(register_16_q), .out(Data02), .sel(RT));  // open: en

  // Notes on the sheet:
  //   AbiMahmood
endmodule

module _1_Bit_ALU (
  input  Cin,
  input  A,
  input  A_Invert,
  input  B,
  input  B_Invert,
  input  [1:0] Select_Bit_Operation,
  output result,
  output Cout
);

  wire adder_1_out, AND_out, multiplexer_1_out, multiplexer_2_out, not_1_out, not_2_out, OR_out, xor_out;

  not not_1 (not_1_out, A);
  not not_2 (not_2_out, B);
  Multiplexer multiplexer_1 (.in0(A), .in1(not_1_out), .out(multiplexer_1_out), .sel(A_Invert));  // open: en
  Multiplexer multiplexer_2 (.in0(B), .in1(not_2_out), .out(multiplexer_2_out), .sel(B_Invert));  // open: en
  and AND (AND_out, multiplexer_1_out, multiplexer_2_out);
  or OR (OR_out, multiplexer_1_out, multiplexer_2_out);
  xor \xor  (xor_out, multiplexer_1_out, multiplexer_2_out);
  Adder #(.width(1)) adder_1 (.a(multiplexer_1_out), .b(multiplexer_2_out), .out(adder_1_out), .cin(Cin), .cout(Cout));
  Multiplexer #(.select(2)) multiplexer_3 (
    .in0(AND_out), .in1(OR_out), .in2(xor_out), .in3(adder_1_out), .out(result), .sel(Select_Bit_Operation));  // open: en

  // Notes on the sheet:
  //   AbiMahmood
endmodule

// ALU
module _16bit_ALUs (
  input  B_Invert,
  input  Cin,
  input  A_Invert,
  input  [1:0] Operation_Code,
  input  [15:0] Input_B,
  input  [15:0] Input_A,
  output [15:0] Result,
  output Zero_Flag,
  output OverFlow
);

  wire n1_bit_alu_1_cout, n1_bit_alu_2_cout, n1_bit_alu_3_cout, n1_bit_alu_4_cout, n1_bit_alu_5_cout,
       n1_bit_alu_6_cout, n1_bit_alu_7_cout, n1_bit_alu_8_cout, n1_bit_alu_9_cout, n1_bit_alu_10_cout,
       n1_bit_alu_11_cout, n1_bit_alu_12_cout, n1_bit_alu_13_cout, n1_bit_alu_14_cout, n1_bit_alu_15_cout,
       n1_bit_alu_16_cout;

  _1_Bit_ALU u_1_bit_alu_1 (
    .A(Input_A[0]), .B(Input_B[0]), .result(Result[0]), .Cout(n1_bit_alu_1_cout), .Cin(Cin),
    .A_Invert(A_Invert), .B_Invert(B_Invert), .Select_Bit_Operation(Operation_Code));
  _1_Bit_ALU u_1_bit_alu_2 (
    .A(Input_A[1]), .B(Input_B[1]), .result(Result[1]), .Cout(n1_bit_alu_2_cout), .Cin(n1_bit_alu_1_cout),
    .A_Invert(A_Invert), .B_Invert(B_Invert), .Select_Bit_Operation(Operation_Code));
  _1_Bit_ALU u_1_bit_alu_3 (
    .A(Input_A[2]), .B(Input_B[2]), .result(Result[2]), .Cout(n1_bit_alu_3_cout), .Cin(n1_bit_alu_2_cout),
    .A_Invert(A_Invert), .B_Invert(B_Invert), .Select_Bit_Operation(Operation_Code));
  _1_Bit_ALU u_1_bit_alu_4 (
    .A(Input_A[3]), .B(Input_B[3]), .result(Result[3]), .Cout(n1_bit_alu_4_cout), .Cin(n1_bit_alu_3_cout),
    .A_Invert(A_Invert), .B_Invert(B_Invert), .Select_Bit_Operation(Operation_Code));
  _1_Bit_ALU u_1_bit_alu_5 (
    .A(Input_A[4]), .B(Input_B[4]), .result(Result[4]), .Cout(n1_bit_alu_5_cout), .Cin(n1_bit_alu_4_cout),
    .A_Invert(A_Invert), .B_Invert(B_Invert), .Select_Bit_Operation(Operation_Code));
  _1_Bit_ALU u_1_bit_alu_6 (
    .A(Input_A[5]), .B(Input_B[5]), .result(Result[5]), .Cout(n1_bit_alu_6_cout), .Cin(n1_bit_alu_5_cout),
    .A_Invert(A_Invert), .B_Invert(B_Invert), .Select_Bit_Operation(Operation_Code));
  _1_Bit_ALU u_1_bit_alu_7 (
    .A(Input_A[6]), .B(Input_B[6]), .result(Result[6]), .Cout(n1_bit_alu_7_cout), .Cin(n1_bit_alu_6_cout),
    .A_Invert(A_Invert), .B_Invert(B_Invert), .Select_Bit_Operation(Operation_Code));
  _1_Bit_ALU u_1_bit_alu_8 (
    .A(Input_A[7]), .B(Input_B[7]), .result(Result[7]), .Cout(n1_bit_alu_8_cout), .Cin(n1_bit_alu_7_cout),
    .A_Invert(A_Invert), .B_Invert(B_Invert), .Select_Bit_Operation(Operation_Code));
  _1_Bit_ALU u_1_bit_alu_9 (
    .A(Input_A[8]), .B(Input_B[8]), .result(Result[8]), .Cout(n1_bit_alu_9_cout), .Cin(n1_bit_alu_8_cout),
    .A_Invert(A_Invert), .B_Invert(B_Invert), .Select_Bit_Operation(Operation_Code));
  _1_Bit_ALU u_1_bit_alu_10 (
    .A(Input_A[9]), .B(Input_B[9]), .result(Result[9]), .Cout(n1_bit_alu_10_cout), .Cin(n1_bit_alu_9_cout),
    .A_Invert(A_Invert), .B_Invert(B_Invert), .Select_Bit_Operation(Operation_Code));
  _1_Bit_ALU u_1_bit_alu_11 (
    .A(Input_A[10]), .B(Input_B[10]), .result(Result[10]), .Cout(n1_bit_alu_11_cout),
    .Cin(n1_bit_alu_10_cout), .A_Invert(A_Invert), .B_Invert(B_Invert), .Select_Bit_Operation(Operation_Code));
  _1_Bit_ALU u_1_bit_alu_12 (
    .A(Input_A[11]), .B(Input_B[11]), .result(Result[11]), .Cout(n1_bit_alu_12_cout),
    .Cin(n1_bit_alu_11_cout), .A_Invert(A_Invert), .B_Invert(B_Invert), .Select_Bit_Operation(Operation_Code));
  _1_Bit_ALU u_1_bit_alu_13 (
    .A(Input_A[12]), .B(Input_B[12]), .result(Result[12]), .Cout(n1_bit_alu_13_cout),
    .Cin(n1_bit_alu_12_cout), .A_Invert(A_Invert), .B_Invert(B_Invert), .Select_Bit_Operation(Operation_Code));
  _1_Bit_ALU u_1_bit_alu_14 (
    .A(Input_A[13]), .B(Input_B[13]), .result(Result[13]), .Cout(n1_bit_alu_14_cout),
    .Cin(n1_bit_alu_13_cout), .A_Invert(A_Invert), .B_Invert(B_Invert), .Select_Bit_Operation(Operation_Code));
  _1_Bit_ALU u_1_bit_alu_15 (
    .A(Input_A[14]), .B(Input_B[14]), .result(Result[14]), .Cout(n1_bit_alu_15_cout),
    .Cin(n1_bit_alu_14_cout), .A_Invert(A_Invert), .B_Invert(B_Invert), .Select_Bit_Operation(Operation_Code));
  _1_Bit_ALU u_1_bit_alu_16 (
    .A(Input_A[15]), .B(Input_B[15]), .result(Result[15]), .Cout(n1_bit_alu_16_cout),
    .Cin(n1_bit_alu_15_cout), .A_Invert(A_Invert), .B_Invert(B_Invert), .Select_Bit_Operation(Operation_Code));
  nor nor_1 (Zero_Flag, Result[0], Result[1], Result[2], Result[3], Result[4], Result[5], Result[6], Result[7], Result[8], Result[9], Result[10], Result[11], Result[12], Result[13], Result[14], Result[15]);
  xor xor_1 (OverFlow, n1_bit_alu_15_cout, n1_bit_alu_16_cout);

  // Notes on the sheet:
  //   AbiMahmood
endmodule
