// Logisim project SingleCycleDatapath.circ as structural Verilog: 5 circuits, main circuit DataPath
// CPU
module DataPath (
  input  RegDST,
  input  RegWrite,
  input  AluSRC,
  input  C_In,
  input  [1:0] ALUopCode,
  input  A_Invert,
  input  B_Invert,
  input  MemWrite,
  input  MemRead,
  input  MemToReg,
  input  Branch,
  input  Beq_Bne_Line,
  output [3:0] OP,
  output [3:0] RD,
  output [3:0] RS,
  output [3:0] RT,
  output [15:0] Result_Out,
  output [15:0] Data1_Out,
  output [15:0] Data2_Out,
  output Overflow
);

  wire alu_16_bit_1_zero_flag, branchcircuit_1_output_to_mux, CLOCK_out;
  wire [3:0] multiplexer_2_out;
  wire [15:0] adder_1_out, adder_2_out, alu_16_bit_1_result, bit_extender_1_out, multiplexer_1_out,
       multiplexer_3_out, PC_q, ram_1_data, shifter_1_out;

  Button CLOCK (.out(CLOCK_out));
  Multiplexer #(.width(16), .enable("false")) multiplexer_1 (
    .in0(adder_1_out), .in1(adder_2_out), .out(multiplexer_1_out), .sel(branchcircuit_1_output_to_mux));
  Register #(.width(16)) PC (.D(multiplexer_1_out), .Q(PC_q), .clk(CLOCK_out));  // open: en, clr
  Adder #(.width(16)) adder_1 (.a(16'h2), .b(PC_q), .out(adder_1_out));  // open: cin, cout
  BranchCircuit branchcircuit_1 (
    .Output_to_MUX(branchcircuit_1_output_to_mux), .Beq_Bne_CU_Line_In(Beq_Bne_Line),
    .Branch_CU_Line_In(Branch), .ALU_Zero_Flag_IN(alu_16_bit_1_zero_flag));
  ROM #(.addrWidth(16), .dataWidth(16)) rom_1 (.addr(PC_q), .data({OP, RD, RS, RT}));  // open: sel
  Multiplexer #(.width(4), .enable("false")) multiplexer_2 (.in0(RT), .in1(RD), .out(multiplexer_2_out), .sel(RegDST));
  RegisterFile registerfile_1 (
    .Write_Data_IN(Result_Out), .Data01(Data1_Out), .Data02(Data2_Out), .RD(RD), .RS(RS), .RT(RT),
    .Clock(CLOCK_out), .RegWrite(RegWrite));
  assign bit_extender_1_out = {{12{multiplexer_2_out[3]}}, multiplexer_2_out};  // Bit_Extender bit_extender_1
  Multiplexer #(.width(16), .enable("false")) multiplexer_3 (
    .in0(Data2_Out), .in1(bit_extender_1_out), .out(multiplexer_3_out), .sel(AluSRC));
  Shifter #(.width(16)) shifter_1 (.in(bit_extender_1_out), .\dist (4'b0001), .out(shifter_1_out));
  ALU_16_bit alu_16_bit_1 (
    .B_Invert(B_Invert), .A_Invert(A_Invert), .Zero_Flag(alu_16_bit_1_zero_flag),
    .Input_B(multiplexer_3_out), .Input_A(Data1_Out), .Operation_Code(ALUopCode), .OverFlow(Overflow),
    .Result(alu_16_bit_1_result), .Cin(C_In));
  Adder #(.width(16)) adder_2 (.a(adder_1_out), .b(shifter_1_out), .out(adder_2_out));  // open: cin, cout
  RAM #(.addrWidth(16), .dataWidth(16), .bus("separate")) ram_1 (
    .addr(alu_16_bit_1_result), .din(Data2_Out), .data(ram_1_data), .str(MemWrite), .clk(CLOCK_out),
    .ld(MemRead));  // open: sel, clr
  Multiplexer #(.width(16), .enable("false")) multiplexer_4 (
    .in0(alu_16_bit_1_result), .in1(ram_1_data), .out(Result_Out), .sel(MemToReg));

  // Notes on the sheet:
  //   Single Cycle Datapath
endmodule

// Register
module RegisterFile (
  input  Clock,
  input  [15:0] Write_Data_IN,
  input  RegWrite,
  input  [3:0] RS,
  input  [3:0] RD,
  input  [3:0] RT,
  output [15:0] Data01,
  output [15:0] Data02
);

  wire and_1_out, and_2_out, and_3_out, and_4_out, and_5_out, and_6_out, and_7_out, and_8_out, and_9_out,
       and_10_out, and_11_out, and_12_out, and_13_out, and_14_out, and_15_out, and_16_out, decoder_1_out0,
       decoder_1_out1, decoder_1_out2, decoder_1_out3, decoder_1_out4, decoder_1_out5, decoder_1_out6,
       decoder_1_out7, decoder_1_out8, decoder_1_out9, decoder_1_out10, decoder_1_out11, decoder_1_out12,
       decoder_1_out13, decoder_1_out14, decoder_1_out15;
  wire [15:0] register_1_q, register_2_q, register_3_q, register_4_q, register_5_q, register_6_q,
       register_7_q, register_8_q, register_9_q, register_10_q, register_11_q, register_12_q, register_13_q,
       register_14_q, register_15_q, register_16_q;

  Decoder #(.select(4)) decoder_1 (
    .out0(decoder_1_out0), .out1(decoder_1_out1), .out2(decoder_1_out2), .out3(decoder_1_out3),
    .out4(decoder_1_out4), .out5(decoder_1_out5), .out6(decoder_1_out6), .out7(decoder_1_out7),
    .out8(decoder_1_out8), .out9(decoder_1_out9), .out10(decoder_1_out10), .out11(decoder_1_out11),
    .out12(decoder_1_out12), .out13(decoder_1_out13), .out14(decoder_1_out14), .out15(decoder_1_out15),
    .sel(RD));  // open: en
  and and_1 (and_1_out, RegWrite, decoder_1_out0);
  and and_2 (and_2_out, RegWrite, decoder_1_out1);
  and and_3 (and_3_out, RegWrite, decoder_1_out2);
  and and_4 (and_4_out, RegWrite, decoder_1_out3);
  and and_5 (and_5_out, RegWrite, decoder_1_out4);
  and and_6 (and_6_out, RegWrite, decoder_1_out5);
  and and_7 (and_7_out, RegWrite, decoder_1_out6);
  and and_8 (and_8_out, RegWrite, decoder_1_out7);
  and and_9 (and_9_out, RegWrite, decoder_1_out8);
  and and_10 (and_10_out, RegWrite, decoder_1_out9);
  and and_11 (and_11_out, RegWrite, decoder_1_out10);
  and and_12 (and_12_out, RegWrite, decoder_1_out11);
  and and_13 (and_13_out, RegWrite, decoder_1_out12);
  and and_14 (and_14_out, RegWrite, decoder_1_out13);
  and and_15 (and_15_out, RegWrite, decoder_1_out14);
  and and_16 (and_16_out, RegWrite, decoder_1_out15);
  Register #(.width(16)) register_1 (.D(Write_Data_IN), .en(and_1_out), .Q(register_1_q), .clk(Clock));  // open: clr
  Register #(.width(16)) register_2 (.D(Write_Data_IN), .en(and_2_out), .Q(register_2_q), .clk(Clock));  // open: clr
  Register #(.width(16)) register_3 (.D(Write_Data_IN), .en(and_3_out), .Q(register_3_q), .clk(Clock));  // open: clr
  Register #(.width(16)) register_4 (.D(Write_Data_IN), .en(and_4_out), .Q(register_4_q), .clk(Clock));  // open: clr
  Register #(.width(16)) register_5 (.D(Write_Data_IN), .en(and_5_out), .Q(register_5_q), .clk(Clock));  // open: clr
  Register #(.width(16)) register_6 (.D(Write_Data_IN), .en(and_6_out), .Q(register_6_q), .clk(Clock));  // open: clr
  Register #(.width(16)) register_7 (.D(Write_Data_IN), .en(and_7_out), .Q(register_7_q), .clk(Clock));  // open: clr
  Register #(.width(16)) register_8 (.D(Write_Data_IN), .en(and_8_out), .Q(register_8_q), .clk(Clock));  // open: clr
  Register #(.width(16)) register_9 (.D(Write_Data_IN), .en(and_9_out), .Q(register_9_q), .clk(Clock));  // open: clr
  Register #(.width(16)) register_10 (.D(Write_Data_IN), .en(and_10_out), .Q(register_10_q), .clk(Clock));  // open: clr
  Register #(.width(16)) register_11 (.D(Write_Data_IN), .en(and_11_out), .Q(register_11_q), .clk(Clock));  // open: clr
  Register #(.width(16)) register_12 (.D(Write_Data_IN), .en(and_12_out), .Q(register_12_q), .clk(Clock));  // open: clr
  Register #(.width(16)) register_13 (.D(Write_Data_IN), .en(and_13_out), .Q(register_13_q), .clk(Clock));  // open: clr
  Register #(.width(16)) register_14 (.D(Write_Data_IN), .en(and_14_out), .Q(register_14_q), .clk(Clock));  // open: clr
  Register #(.width(16)) register_15 (.D(Write_Data_IN), .en(and_15_out), .Q(register_15_q), .clk(Clock));  // open: clr
  Register #(.width(16)) register_16 (.D(Write_Data_IN), .en(and_16_out), .Q(register_16_q), .clk(Clock));  // open: clr
  Multiplexer #(.select(4), .width(16)) multiplexer_1 (
    .in0(register_1_q), .in1(register_2_q), .in2(register_3_q), .in3(register_4_q), .in4(register_5_q),
    .in5(register_6_q), .in6(register_7_q), .in7(register_8_q), .in8(register_9_q), .in9(register_10_q),
    .in10(register_11_q), .in11(register_12_q), .in12(register_13_q), .in13(register_14_q),
    .in14(register_15_q), .in15(register_16_q), .out(Data01), .sel(RS));  // open: en
  Multiplexer #(.select(4), .width(16)) multiplexer_2 (
    .in0(register_1_q), .in1(register_2_q), .in2(register_3_q), .in3(register_4_q), .in4(register_5_q),
    .in5(register_6_q), .in6(register_7_q), .in7(register_8_q), .in8(register_9_q), .in9(register_10_q),
    .in10(register_11_q), .in11(register_12_q), .in12(register_13_q), .in13(register_14_q),
    .in14(register_15_q), .in15(register_16_q), .out(Data02), .sel(RT));  // open: en

  // Notes on the sheet:
  //   Register Files
endmodule

module BranchCircuit (
  input  Beq_Bne_CU_Line_In,
  input  Branch_CU_Line_In,
  input  ALU_Zero_Flag_IN,
  output Output_to_MUX
);

  wire not_1_out, xor_1_out;

  and and_1 (Output_to_MUX, Beq_Bne_CU_Line_In, not_1_out);
  not not_1 (not_1_out, xor_1_out);
  xor xor_1 (xor_1_out, Branch_CU_Line_In, ALU_Zero_Flag_IN);

  // Notes on the sheet:
  //   Instructions    Branch    ALUZ    BCU   Output    invert
  //   BNE                    0             0        1         1            0
  //   BNE                    0             1        1         0            1
  //   BEQ                    1             0        1         0            1
  //   BEQ                    1             1        1         1            0
  //   Other ins             0             0        0         0
  //   Other ins             0             1        0         0
  //   Truth Table 
  //   AND Gate
  //   Xor + Not Gate
endmodule

// ALU
module ALU_16_bit (
  input  Cin,
  input  B_Invert,
  input  A_Invert,
  input  [1:0] Operation_Code,
  input  [15:0] Input_B,
  input  [15:0] Input_A,
  output [15:0] Result,
  output Zero_Flag,
  output OverFlow
);

  wire alu_1_bit_1_cout, alu_1_bit_2_cout, alu_1_bit_3_cout, alu_1_bit_4_cout, alu_1_bit_5_cout,
       alu_1_bit_6_cout, alu_1_bit_7_cout, alu_1_bit_8_cout, alu_1_bit_9_cout, alu_1_bit_10_cout,
       alu_1_bit_11_cout, alu_1_bit_12_cout, alu_1_bit_13_cout, alu_1_bit_14_cout, alu_1_bit_15_cout,
       alu_1_bit_16_cout;

  ALU_1_bit alu_1_bit_1 (
    .A(Input_A[0]), .B(Input_B[0]), .Cout(alu_1_bit_1_cout), .Cin(Cin), .A_Invert(A_Invert),
    .B_Invert(B_Invert), .Select_Bit_Operation(Operation_Code), .Result(Result[0]));
  ALU_1_bit alu_1_bit_2 (
    .A(Input_A[1]), .B(Input_B[1]), .Cout(alu_1_bit_2_cout), .Cin(alu_1_bit_1_cout), .A_Invert(A_Invert),
    .B_Invert(B_Invert), .Select_Bit_Operation(Operation_Code), .Result(Result[1]));
  ALU_1_bit alu_1_bit_3 (
    .A(Input_A[2]), .B(Input_B[2]), .Cout(alu_1_bit_3_cout), .Cin(alu_1_bit_2_cout), .A_Invert(A_Invert),
    .B_Invert(B_Invert), .Select_Bit_Operation(Operation_Code), .Result(Result[2]));
  ALU_1_bit alu_1_bit_4 (
    .A(Input_A[3]), .B(Input_B[3]), .Cout(alu_1_bit_4_cout), .Cin(alu_1_bit_3_cout), .A_Invert(A_Invert),
    .B_Invert(B_Invert), .Select_Bit_Operation(Operation_Code), .Result(Result[3]));
  ALU_1_bit alu_1_bit_5 (
    .A(Input_A[4]), .B(Input_B[4]), .Cout(alu_1_bit_5_cout), .Cin(alu_1_bit_4_cout), .A_Invert(A_Invert),
    .B_Invert(B_Invert), .Select_Bit_Operation(Operation_Code), .Result(Result[4]));
  ALU_1_bit alu_1_bit_6 (
    .A(Input_A[5]), .B(Input_B[5]), .Cout(alu_1_bit_6_cout), .Cin(alu_1_bit_5_cout), .A_Invert(A_Invert),
    .B_Invert(B_Invert), .Select_Bit_Operation(Operation_Code), .Result(Result[5]));
  ALU_1_bit alu_1_bit_7 (
    .A(Input_A[6]), .B(Input_B[6]), .Cout(alu_1_bit_7_cout), .Cin(alu_1_bit_6_cout), .A_Invert(A_Invert),
    .B_Invert(B_Invert), .Select_Bit_Operation(Operation_Code), .Result(Result[6]));
  ALU_1_bit alu_1_bit_8 (
    .A(Input_A[7]), .B(Input_B[7]), .Cout(alu_1_bit_8_cout), .Cin(alu_1_bit_7_cout), .A_Invert(A_Invert),
    .B_Invert(B_Invert), .Select_Bit_Operation(Operation_Code), .Result(Result[7]));
  ALU_1_bit alu_1_bit_9 (
    .A(Input_A[8]), .B(Input_B[8]), .Cout(alu_1_bit_9_cout), .Cin(alu_1_bit_8_cout), .A_Invert(A_Invert),
    .B_Invert(B_Invert), .Select_Bit_Operation(Operation_Code), .Result(Result[8]));
  ALU_1_bit alu_1_bit_10 (
    .A(Input_A[9]), .B(Input_B[9]), .Cout(alu_1_bit_10_cout), .Cin(alu_1_bit_9_cout), .A_Invert(A_Invert),
    .B_Invert(B_Invert), .Select_Bit_Operation(Operation_Code), .Result(Result[9]));
  ALU_1_bit alu_1_bit_11 (
    .A(Input_A[10]), .B(Input_B[10]), .Cout(alu_1_bit_11_cout), .Cin(alu_1_bit_10_cout), .A_Invert(A_Invert),
    .B_Invert(B_Invert), .Select_Bit_Operation(Operation_Code), .Result(Result[10]));
  ALU_1_bit alu_1_bit_12 (
    .A(Input_A[11]), .B(Input_B[11]), .Cout(alu_1_bit_12_cout), .Cin(alu_1_bit_11_cout), .A_Invert(A_Invert),
    .B_Invert(B_Invert), .Select_Bit_Operation(Operation_Code), .Result(Result[11]));
  ALU_1_bit alu_1_bit_13 (
    .A(Input_A[12]), .B(Input_B[12]), .Cout(alu_1_bit_13_cout), .Cin(alu_1_bit_12_cout), .A_Invert(A_Invert),
    .B_Invert(B_Invert), .Select_Bit_Operation(Operation_Code), .Result(Result[12]));
  ALU_1_bit alu_1_bit_14 (
    .A(Input_A[13]), .B(Input_B[13]), .Cout(alu_1_bit_14_cout), .Cin(alu_1_bit_13_cout), .A_Invert(A_Invert),
    .B_Invert(B_Invert), .Select_Bit_Operation(Operation_Code), .Result(Result[13]));
  ALU_1_bit alu_1_bit_15 (
    .A(Input_A[14]), .B(Input_B[14]), .Cout(alu_1_bit_15_cout), .Cin(alu_1_bit_14_cout), .A_Invert(A_Invert),
    .B_Invert(B_Invert), .Select_Bit_Operation(Operation_Code), .Result(Result[14]));
  ALU_1_bit alu_1_bit_16 (
    .A(Input_A[15]), .B(Input_B[15]), .Cout(alu_1_bit_16_cout), .Cin(alu_1_bit_15_cout), .A_Invert(A_Invert),
    .B_Invert(B_Invert), .Select_Bit_Operation(Operation_Code), .Result(Result[15]));
  nor nor_1 (Zero_Flag, Result[0], Result[1], Result[2], Result[3], Result[4], Result[5], Result[6], Result[7], Result[8], Result[9], Result[10], Result[11], Result[12], Result[13], Result[14], Result[15]);
  xor xor_1 (OverFlow, alu_1_bit_15_cout, alu_1_bit_16_cout);

  // Notes on the sheet:
  //   ALU 16 BIT
endmodule

// 1 Bit ALU
module ALU_1_bit (
  input  Cin,
  input  A,
  input  A_Invert,
  input  B,
  input  B_Invert,
  input  [1:0] Select_Bit_Operation,
  output Result,
  output Cout
);

  wire adder_1_out, AND_out, multiplexer_1_out, multiplexer_2_out, not_1_out, not_2_out, OR_out, xor_out;

  Multiplexer multiplexer_1 (.in0(A), .in1(not_1_out), .out(multiplexer_1_out), .sel(A_Invert));  // open: en
  not not_1 (not_1_out, A);
  not not_2 (not_2_out, B);
  Multiplexer multiplexer_2 (.in0(B), .in1(not_2_out), .out(multiplexer_2_out), .sel(B_Invert));  // open: en
  and AND (AND_out, multiplexer_1_out, multiplexer_2_out);
  or OR (OR_out, multiplexer_1_out, multiplexer_2_out);
  xor \xor  (xor_out, multiplexer_1_out, multiplexer_2_out);
  Adder #(.width(1)) adder_1 (.a(multiplexer_1_out), .b(multiplexer_2_out), .out(adder_1_out), .cin(Cin), .cout(Cout));
  Multiplexer #(.select(2)) multiplexer_3 (
    .in0(AND_out), .in1(OR_out), .in2(xor_out), .in3(adder_1_out), .out(Result), .sel(Select_Bit_Operation));  // open: en

  // Notes on the sheet:
  //   ALU 1BIT
endmodule
