// Logisim project Pipeline Datapath With FU (VERSION 2).circ as structural Verilog: 8 circuits, main circuit DataPath
// CPU :)
module DataPath (
  output [1:0] out_1,
  output [3:0] OP,
  output [3:0] RD,
  output [3:0] RS,
  output [3:0] RT,
  output [15:0] out_6,
  output [15:0] Result_Out,
  output [15:0] Data1_Out,
  output [15:0] Data2_Out,
  output Overflow
);

  wire alu_16_bit_1_overflow, alu_16_bit_1_zero_flag, branchcircuit_1_output_to_mux, CLOCK_out,
       maincontrolunit_1_a_invert, maincontrolunit_1_alusrc, maincontrolunit_1_beq_bne_line,
       maincontrolunit_1_binvert, maincontrolunit_1_branch, maincontrolunit_1_memread,
       maincontrolunit_1_memtoreg, maincontrolunit_1_memwrite, maincontrolunit_1_regdst,
       maincontrolunit_1_regwrite, register_3_q, register_4_q, register_5_q, register_6_q, register_7_q,
       register_8_q, register_9_q, register_10_q, register_12_q, register_20_q, register_21_q, register_22_q,
       register_23_q, register_24_q, register_25_q, register_27_q, register_29_q, register_32_q,
       register_33_q;
  wire [1:0] forward_unit_1_forwardmuxa, forward_unit_1_forwardmuxb, maincontrolunit_1_aluop;
  wire [3:0] register_2_q, register_17_q, register_18_q, register_19_q, register_31_q, register_37_q;
  wire [15:0] adder_1_out, adder_2_out, alu_16_bit_1_result, bit_extender_1_out, multiplexer_1_out,
       multiplexer_3_out, multiplexer_4_out, multiplexer_5_out, PC_q, ram_1_data, register_1_q,
       register_13_q, register_14_q, register_15_q, register_16_q, register_26_q, register_30_q,
       register_34_q, register_35_q, rom_1_data, shifter_1_out;

  Multiplexer #(.width(16), .enable("false")) multiplexer_1 (
    .in0(adder_1_out), .in1(register_26_q), .out(multiplexer_1_out), .sel(branchcircuit_1_output_to_mux));
  Register #(.width(16)) PC (.D(multiplexer_1_out), .Q(PC_q), .clk(CLOCK_out));  // open: en, clr
  Button CLOCK (.out(CLOCK_out));
  Hazard_Detection_Unit hazard_detection_unit_1 ();  // open: IF___ID_RegisterRs, ID___EX_RegisterRt, IF___ID_RegisterRt, ID___EX_MemRead, FlushControl, PCWrite, IF___ID_Write
  Adder #(.width(16)) adder_1 (.a(16'h1), .b(PC_q), .out(adder_1_out));  // open: cin, cout
  ROM #(.addrWidth(16), .dataWidth(16)) rom_1 (.addr(PC_q), .data(rom_1_data));  // open: sel
  Register #(.width(16)) register_1 (.D(adder_1_out), .Q(register_1_q), .clk(CLOCK_out));  // open: en, clr
  Register #(.width(16)) register_2 (.D(rom_1_data), .Q({OP, RD, RS, register_2_q}), .clk(CLOCK_out));  // open: en, clr
  MainControlUnit maincontrolunit_1 (
    .Ins_Input(OP), .RegWrite(maincontrolunit_1_regwrite), .ALUsrc(maincontrolunit_1_alusrc),
    .Binvert(maincontrolunit_1_binvert), .A_invert(maincontrolunit_1_a_invert),
    .MemToReg(maincontrolunit_1_memtoreg), .MemRead(maincontrolunit_1_memread),
    .MemWrite(maincontrolunit_1_memwrite), .Branch(maincontrolunit_1_branch),
    .ALUop(maincontrolunit_1_aluop), .BEQ_BNE_Line(maincontrolunit_1_beq_bne_line),
    .REGDst(maincontrolunit_1_regdst));
  Multiplexer #(.width(4), .enable("false")) multiplexer_2 (
    .in0(register_2_q), .in1(RD), .out(RT), .sel(maincontrolunit_1_regdst));
  RegisterFile registerfile_1 (
    .Write_Data_IN(Result_Out), .Data01(Data1_Out), .Data02(Data2_Out), .RD(register_37_q), .RS(RS), .RT(RT),
    .Clock(CLOCK_out), .RegWrite(register_32_q));
  assign bit_extender_1_out = {{12{register_2_q[3]}}, register_2_q};  // Bit_Extender bit_extender_1
  Register #(.width(1)) register_3 (
    .D(maincontrolunit_1_beq_bne_line), .Q(register_3_q), .clk(CLOCK_out));  // open: en, clr
  Register #(.width(1)) register_4 (
    .D(maincontrolunit_1_regwrite), .Q(register_4_q), .clk(CLOCK_out));  // open: en, clr
  Register #(.width(1)) register_5 (
    .D(maincontrolunit_1_memtoreg), .Q(register_5_q), .clk(CLOCK_out));  // open: en, clr
  Register #(.width(1)) register_6 (.D(maincontrolunit_1_memread), .Q(register_6_q), .clk(CLOCK_out));  // open: en, clr
  Register #(.width(1)) register_7 (
    .D(maincontrolunit_1_memwrite), .Q(register_7_q), .clk(CLOCK_out));  // open: en, clr
  Register #(.width(1)) register_8 (.D(maincontrolunit_1_branch), .Q(register_8_q), .clk(CLOCK_out));  // open: en, clr
  Register #(.width(1)) register_9 (.D(maincontrolunit_1_binvert), .Q(register_9_q), .clk(CLOCK_out));  // open: en, clr
  Register #(.width(1)) register_10 (
    .D(maincontrolunit_1_a_invert), .Q(register_10_q), .clk(CLOCK_out));  // open: en, clr
  Register #(.width(2)) register_11 (.D(maincontrolunit_1_aluop), .Q(out_1), .clk(CLOCK_out));  // open: en, clr
  Register #(.width(1)) register_12 (
    .D(maincontrolunit_1_alusrc), .Q(register_12_q), .clk(CLOCK_out));  // open: en, clr
  Register #(.width(16)) register_13 (.D(register_1_q), .Q(register_13_q), .clk(CLOCK_out));  // open: en, clr
  Register #(.width(16)) register_14 (.D(Data1_Out), .Q(register_14_q), .clk(CLOCK_out));  // open: en, clr
  Register #(.width(16)) register_15 (.D(Data2_Out), .Q(register_15_q), .clk(CLOCK_out));  // open: en, clr
  Register #(.width(16)) register_16 (.D(bit_extender_1_out), .Q(register_16_q), .clk(CLOCK_out));  // open: en, clr
  Register #(.width(4)) register_17 (.D(RS), .Q(register_17_q), .clk(CLOCK_out));  // open: en, clr
  Register #(.width(4)) register_18 (.D(register_2_q), .Q(register_18_q), .clk(CLOCK_out));  // open: en, clr
  Register #(.width(4)) register_19 (.D(RD), .Q(register_19_q), .clk(CLOCK_out));  // open: en, clr
  Multiplexer #(.width(16), .enable("false")) multiplexer_3 (
    .in0(register_15_q), .in1(register_16_q), .out(multiplexer_3_out), .sel(register_12_q));
  Multiplexer #(.select(2), .width(16), .enable("false")) multiplexer_4 (
    .in0(register_14_q), .in1(Result_Out), .in2(out_6), .out(multiplexer_4_out),
    .sel(forward_unit_1_forwardmuxa));  // open: in3
  Multiplexer #(.select(2), .width(16), .enable("false")) multiplexer_5 (
    .in0(multiplexer_3_out), .in1(Result_Out), .in2(out_6), .out(multiplexer_5_out),
    .sel(forward_unit_1_forwardmuxb));  // open: in3
  Shifter #(.width(16)) shifter_1 (.in(register_16_q), .\dist (4'b0001), .out(shifter_1_out));
  ALU_16_bit alu_16_bit_1 (
    .B_Invert(register_9_q), .A_Invert(register_10_q), .Zero_Flag(alu_16_bit_1_zero_flag),
    .Input_B(multiplexer_5_out), .Input_A(multiplexer_4_out), .Operation_Code(out_1),
    .OverFlow(alu_16_bit_1_overflow), .Result(alu_16_bit_1_result), .Cin(register_9_q));
  Adder #(.width(16)) adder_2 (.a(register_13_q), .b(shifter_1_out), .out(adder_2_out));  // open: cin, cout
  Forward_Unit forward_unit_1 (
    .EX_MEM_RegWrite(register_21_q), .EX_MEM_RegisterRd(register_31_q), .ID_EX_Rs(register_17_q),
    .ID_EX_Rt(register_18_q), .MEM_WB_RegisterRd(register_37_q), .MEM_WB_RegWrite(register_32_q),
    .ForwardMUXA(forward_unit_1_forwardmuxa), .ForwardMUXB(forward_unit_1_forwardmuxb));
  Register #(.width(1)) register_20 (.D(register_3_q), .Q(register_20_q), .clk(CLOCK_out));  // open: en, clr
  Register #(.width(1)) register_21 (.D(register_4_q), .Q(register_21_q), .clk(CLOCK_out));  // open: en, clr
  Register #(.width(1)) register_22 (.D(register_5_q), .Q(register_22_q), .clk(CLOCK_out));  // open: en, clr
  Register #(.width(1)) register_23 (.D(register_6_q), .Q(register_23_q), .clk(CLOCK_out));  // open: en, clr
  Register #(.width(1)) register_24 (.D(register_7_q), .Q(register_24_q), .clk(CLOCK_out));  // open: en, clr
  Register #(.width(1)) register_25 (.D(register_8_q), .Q(register_25_q), .clk(CLOCK_out));  // open: en, clr
  Register #(.width(16)) register_26 (.D(adder_2_out), .Q(register_26_q), .clk(CLOCK_out));  // open: en, clr
  Register #(.width(1)) register_27 (.D(alu_16_bit_1_zero_flag), .Q(register_27_q), .clk(CLOCK_out));  // open: en, clr
  Register #(.width(16)) register_28 (.D(alu_16_bit_1_result), .Q(out_6), .clk(CLOCK_out));  // open: en, clr
  Register #(.width(1)) register_29 (.D(alu_16_bit_1_overflow), .Q(register_29_q), .clk(CLOCK_out));  // open: en, clr
  Register #(.width(16)) register_30 (.D(register_15_q), .Q(register_30_q), .clk(CLOCK_out));  // open: en, clr
  Register #(.width(4)) register_31 (.D(register_19_q), .Q(register_31_q), .clk(CLOCK_out));  // open: en, clr
  BranchCircuit branchcircuit_1 (
    .Output_to_MUX(branchcircuit_1_output_to_mux), .Beq_Bne_CU_Line_In(register_20_q),
    .Branch_CU_Line_In(register_25_q), .ALU_Zero_Flag_IN(register_27_q));
  RAM #(.addrWidth(16), .dataWidth(16), .bus("separate")) ram_1 (
    .addr(out_6), .din(register_30_q), .data(ram_1_data), .str(register_24_q), .clk(CLOCK_out),
    .ld(register_23_q));  // open: sel, clr
  Register #(.width(1)) register_32 (.D(register_21_q), .Q(register_32_q), .clk(CLOCK_out));  // open: en, clr
  Register #(.width(1)) register_33 (.D(register_22_q), .Q(register_33_q), .clk(CLOCK_out));  // open: en, clr
  Register #(.width(16)) register_34 (.D(out_6), .Q(register_34_q), .clk(CLOCK_out));  // open: en, clr
  Register #(.width(16)) register_35 (.D(ram_1_data), .Q(register_35_q), .clk(CLOCK_out));  // open: en, clr
  Register #(.width(1)) register_36 (.D(register_29_q), .Q(Overflow), .clk(CLOCK_out));  // open: en, clr
  Register #(.width(4)) register_37 (.D(register_31_q), .Q(register_37_q), .clk(CLOCK_out));  // open: en, clr
  Multiplexer #(.width(16), .enable("false")) multiplexer_6 (
    .in0(register_34_q), .in1(register_35_q), .out(Result_Out), .sel(register_33_q));

  // Notes on the sheet:
  //   Limitations
  //   # Only Works some general R / I types 
  //   # Destination Register can not be repeated
  //   contents of rom_1 (hex, n*v repeats v):
  //   8111 211 322 433 1532 1654 3755 d971
  //   IF/ID 32Bits
  //   ID/EX
  //   Pipeline Datapath
  //   EX/MEM 
  //   MEM/WB 
endmodule

module MainControlUnit (
  input  [3:0] Ins_Input,
  output RegWrite,
  output ALUsrc,
  output Binvert,
  output A_invert,
  output MemToReg,
  output MemRead,
  output MemWrite,
  output Branch,
  output REGDst,
  output [1:0] ALUop,
  output BEQ_BNE_Line
);

  wire ADD_0000_out, ADDi_1000_out, AND_0100_out, ANDi_1100_out, BNE_1111_out, NAND_0110_out, noOp_out,
       Nor_0010_out, OR_0011_out, ORi_1011_out, Sub_0001_out, XOR_0101_out, XORi_1101_out;

  and ADD_0000 (ADD_0000_out, ~Ins_Input[3], ~Ins_Input[2], ~Ins_Input[1], ~Ins_Input[0]);  // AND_Gate
  and Sub_0001 (Sub_0001_out, ~Ins_Input[3], ~Ins_Input[2], ~Ins_Input[1], Ins_Input[0]);  // AND_Gate
  and Nor_0010 (Nor_0010_out, ~Ins_Input[3], ~Ins_Input[2], Ins_Input[1], ~Ins_Input[0]);  // AND_Gate
  and OR_0011 (OR_0011_out, ~Ins_Input[3], ~Ins_Input[2], Ins_Input[1], Ins_Input[0]);  // AND_Gate
  and AND_0100 (AND_0100_out, ~Ins_Input[3], Ins_Input[2], ~Ins_Input[1], ~Ins_Input[0]);  // AND_Gate
  and XOR_0101 (XOR_0101_out, ~Ins_Input[3], Ins_Input[2], ~Ins_Input[1], Ins_Input[0]);  // AND_Gate
  and NAND_0110 (NAND_0110_out, ~Ins_Input[3], Ins_Input[2], Ins_Input[1], ~Ins_Input[0]);  // AND_Gate
  and noOp (noOp_out, ~Ins_Input[3], Ins_Input[2], Ins_Input[1], Ins_Input[0]);  // AND_Gate
  and ADDi_1000 (ADDi_1000_out, Ins_Input[3], ~Ins_Input[2], ~Ins_Input[1], ~Ins_Input[0]);  // AND_Gate
  and lw_1001 (MemRead, Ins_Input[3], ~Ins_Input[2], ~Ins_Input[1], Ins_Input[0]);  // AND_Gate
  and sw_1010 (MemWrite, Ins_Input[3], ~Ins_Input[2], Ins_Input[1], ~Ins_Input[0]);  // AND_Gate
  and ORi_1011 (ORi_1011_out, Ins_Input[3], ~Ins_Input[2], Ins_Input[1], Ins_Input[0]);  // AND_Gate
  and ANDi_1100 (ANDi_1100_out, Ins_Input[3], Ins_Input[2], ~Ins_Input[1], ~Ins_Input[0]);  // AND_Gate
  and XORi_1101 (XORi_1101_out, Ins_Input[3], Ins_Input[2], ~Ins_Input[1], Ins_Input[0]);  // AND_Gate
  and BEQ_1110 (Branch, Ins_Input[3], Ins_Input[2], Ins_Input[1], ~Ins_Input[0]);  // AND_Gate
  and BNE_1111 (BNE_1111_out, Ins_Input[3], Ins_Input[2], Ins_Input[1], Ins_Input[0]);
  or or_1 (RegWrite, ADD_0000_out, Sub_0001_out, Nor_0010_out, OR_0011_out, AND_0100_out, XOR_0101_out, NAND_0110_out, noOp_out, ADDi_1000_out, MemRead, ORi_1011_out, ANDi_1100_out, XORi_1101_out);
  or or_2 (ALUsrc, noOp_out, ADDi_1000_out, MemRead, MemWrite, ORi_1011_out, ANDi_1100_out, XORi_1101_out);
  or or_3 (Binvert, NAND_0110_out, Sub_0001_out, Nor_0010_out, noOp_out, Branch, BNE_1111_out);
  or or_4 (A_invert, NAND_0110_out, Nor_0010_out);
  or or_5 (REGDst, Branch, MemWrite, BNE_1111_out);
  or _1st (ALUop[1], ADD_0000_out, Sub_0001_out, XOR_0101_out, noOp_out, ADDi_1000_out, MemRead, MemWrite, XORi_1101_out, Branch, BNE_1111_out);
  or _2nd (ALUop[0], ADD_0000_out, Sub_0001_out, OR_0011_out, noOp_out, ADDi_1000_out, NAND_0110_out, MemRead, MemWrite, ORi_1011_out, Branch, BNE_1111_out);
  or or_6 (BEQ_BNE_Line, BNE_1111_out, Branch);

  assign MemToReg = MemRead;

  // Notes on the sheet:
  //   AbdullahMahmood
  //   0     1     2      3     4       5      6      7      8     9     10     11    12    13     14    15  
  //   Main Control Unit
endmodule

module BranchCircuit (
  input  Beq_Bne_CU_Line_In,
  input  Branch_CU_Line_In,
  input  ALU_Zero_Flag_IN,
  output Output_to_MUX
);

  wire not_1_out, xor_1_out;

  and and_1 (Output_to_MUX, Beq_Bne_CU_Line_In, not_1_out);
  not not_1 (not_1_out, xor_1_out);
  xor xor_1 (xor_1_out, Branch_CU_Line_In, ALU_Zero_Flag_IN);

  // Notes on the sheet:
  //   Branch Circuit
  //   Instructions    Branch    ALUZ    BCU   Output    invert
  //   BNE                    0             0        1         1            0
  //   BNE                    0             1        1         0            1
  //   BEQ                    1             0        1         0            1
  //   BEQ                    1             1        1         1            0
  //   Other ins             0             0        0         0
  //   Other ins             0             1        0         0
  //   Truth Table 
  //   AND Gate
  //   Xor + Not Gate
  //   AbdullahMahmood
endmodule

// Registers
module RegisterFile (
  input  Clock,
  input  [15:0] Write_Data_IN,
  input  RegWrite,
  input  [3:0] RS,
  input  [3:0] RD,
  input  [3:0] RT,
  output [15:0] Data01,
  output [15:0] Data02
);

  wire and_1_out, and_2_out, and_3_out, and_4_out, and_5_out, and_6_out, and_7_out, and_8_out, and_9_out,
       and_10_out, and_11_out, and_12_out, and_13_out, and_14_out, and_15_out, and_16_out, decoder_1_out0,
       decoder_1_out1, decoder_1_out2, decoder_1_out3, decoder_1_out4, decoder_1_out5, decoder_1_out6,
       decoder_1_out7, decoder_1_out8, decoder_1_out9, decoder_1_out10, decoder_1_out11, decoder_1_out12,
       decoder_1_out13, decoder_1_out14, decoder_1_out15;
  wire [15:0] register_1_q, register_2_q, register_3_q, register_4_q, register_5_q, register_6_q,
       register_7_q, register_8_q, register_9_q, register_10_q, register_11_q, register_12_q, register_13_q,
       register_14_q, register_15_q, register_16_q;

  Decoder #(.select(4)) decoder_1 (
    .out0(decoder_1_out0), .out1(decoder_1_out1), .out2(decoder_1_out2), .out3(decoder_1_out3),
    .out4(decoder_1_out4), .out5(decoder_1_out5), .out6(decoder_1_out6), .out7(decoder_1_out7),
    .out8(decoder_1_out8), .out9(decoder_1_out9), .out10(decoder_1_out10), .out11(decoder_1_out11),
    .out12(decoder_1_out12), .out13(decoder_1_out13), .out14(decoder_1_out14), .out15(decoder_1_out15),
    .sel(RD));  // open: en
  and and_1 (and_1_out, RegWrite, decoder_1_out0);
  and and_2 (and_2_out, RegWrite, decoder_1_out1);
  and and_3 (and_3_out, RegWrite, decoder_1_out2);
  and and_4 (and_4_out, RegWrite, decoder_1_out3);
  and and_5 (and_5_out, RegWrite, decoder_1_out4);
  and and_6 (and_6_out, RegWrite, decoder_1_out5);
  and and_7 (and_7_out, RegWrite, decoder_1_out6);
  and and_8 (and_8_out, RegWrite, decoder_1_out7);
  and and_9 (and_9_out, RegWrite, decoder_1_out8);
  and and_10 (and_10_out, RegWrite, decoder_1_out9);
  and and_11 (and_11_out, RegWrite, decoder_1_out10);
  and and_12 (and_12_out, RegWrite, decoder_1_out11);
  and and_13 (and_13_out, RegWrite, decoder_1_out12);
  and and_14 (and_14_out, RegWrite, decoder_1_out13);
  and and_15 (and_15_out, RegWrite, decoder_1_out14);
  and and_16 (and_16_out, RegWrite, decoder_1_out15);
  Register #(.width(16)) register_1 (.D(Write_Data_IN), .en(and_1_out), .Q(register_1_q), .clk(Clock));  // open: clr
  Register #(.width(16)) register_2 (.D(Write_Data_IN), .en(and_2_out), .Q(register_2_q), .clk(Clock));  // open: clr
  Register #(.width(16)) register_3 (.D(Write_Data_IN), .en(and_3_out), .Q(register_3_q), .clk(Clock));  // open: clr
  Register #(.width(16)) register_4 (.D(Write_Data_IN), .en(and_4_out), .Q(register_4_q), .clk(Clock));  // open: clr
  Register #(.width(16)) register_5 (.D(Write_Data_IN), .en(and_5_out), .Q(register_5_q), .clk(Clock));  // open: clr
  Register #(.width(16)) register_6 (.D(Write_Data_IN), .en(and_6_out), .Q(register_6_q), .clk(Clock));  // open: clr
  Register #(.width(16)) register_7 (.D(Write_Data_IN), .en(and_7_out), .Q(register_7_q), .clk(Clock));  // open: clr
  Register #(.width(16)) register_8 (.D(Write_Data_IN), .en(and_8_out), .Q(register_8_q), .clk(Clock));  // open: clr
  Register #(.width(16)) register_9 (.D(Write_Data_IN), .en(and_9_out), .Q(register_9_q), .clk(Clock));  // open: clr
  Register #(.width(16)) register_10 (.D(Write_Data_IN), .en(and_10_out), .Q(register_10_q), .clk(Clock));  // open: clr
  Register #(.width(16)) register_11 (.D(Write_Data_IN), .en(and_11_out), .Q(register_11_q), .clk(Clock));  // open: clr
  Register #(.width(16)) register_12 (.D(Write_Data_IN), .en(and_12_out), .Q(register_12_q), .clk(Clock));  // open: clr
  Register #(.width(16)) register_13 (.D(Write_Data_IN), .en(and_13_out), .Q(register_13_q), .clk(Clock));  // open: clr
  Register #(.width(16)) register_14 (.D(Write_Data_IN), .en(and_14_out), .Q(register_14_q), .clk(Clock));  // open: clr
  Register #(.width(16)) register_15 (.D(Write_Data_IN), .en(and_15_out), .Q(register_15_q), .clk(Clock));  // open: clr
  Register #(.width(16)) register_16 (.D(Write_Data_IN), .en(and_16_out), .Q(register_16_q), .clk(Clock));  // open: clr
  Multiplexer #(.select(4), .width(16)) multiplexer_1 (
    .in0(register_1_q), .in1(register_2_q), .in2(register_3_q), .in3(register_4_q), .in4(register_5_q),
    .in5(register_6_q), .in6(register_7_q), .in7(register_8_q), .in8(register_9_q), .in9(register_10_q),
    .in10(register_11_q), .in11(register_12_q), .in12(register_13_q), .in13(register_14_q),
    .in14(register_15_q), .in15(register_16_q), .out(Data01), .sel(RS));  // open: en
  Multiplexer #(.select(4), .width(16)) multiplexer_2 (
    .in0(register_1_q), .in1(register_2_q), .in2(register_3_q), .in3(register_4_q), .in4(register_5_q),
    .in5(register_6_q), .in6(register_7_q), .in7(register_8_q), .in8(register_9_q), .in9(register_10_q),
    .in10(register_11_q), .in11(register_12_q), .in12(register_13_q), .in13(register_14_q),
    .in14(register_15_q), .in15(register_16_q), .out(Data02), .sel(RT));  // open: en

  // Notes on the sheet:
  //   AbdullahMahmood
  //   Register Files
endmodule

module ALU_16_bit (
  input  Cin,
  input  B_Invert,
  input  A_Invert,
  input  [1:0] Operation_Code,
  input  [15:0] Input_B,
  input  [15:0] Input_A,
  output [15:0] Result,
  output Zero_Flag,
  output OverFlow
);

  wire alu_1_bit_1_cout, alu_1_bit_2_cout, alu_1_bit_3_cout, alu_1_bit_4_cout, alu_1_bit_5_cout,
       alu_1_bit_6_cout, alu_1_bit_7_cout, alu_1_bit_8_cout, alu_1_bit_9_cout, alu_1_bit_10_cout,
       alu_1_bit_11_cout, alu_1_bit_12_cout, alu_1_bit_13_cout, alu_1_bit_14_cout, alu_1_bit_15_cout,
       alu_1_bit_16_cout;

  ALU_1_bit alu_1_bit_1 (
    .A(Input_A[0]), .B(Input_B[0]), .Cout(alu_1_bit_1_cout), .Cin(Cin), .A_Invert(A_Invert),
    .B_Invert(B_Invert), .Select_Bit_Operation(Operation_Code), .Result(Result[0]));
  ALU_1_bit alu_1_bit_2 (
    .A(Input_A[1]), .B(Input_B[1]), .Cout(alu_1_bit_2_cout), .Cin(alu_1_bit_1_cout), .A_Invert(A_Invert),
    .B_Invert(B_Invert), .Select_Bit_Operation(Operation_Code), .Result(Result[1]));
  ALU_1_bit alu_1_bit_3 (
    .A(Input_A[2]), .B(Input_B[2]), .Cout(alu_1_bit_3_cout), .Cin(alu_1_bit_2_cout), .A_Invert(A_Invert),
    .B_Invert(B_Invert), .Select_Bit_Operation(Operation_Code), .Result(Result[2]));
  ALU_1_bit alu_1_bit_4 (
    .A(Input_A[3]), .B(Input_B[3]), .Cout(alu_1_bit_4_cout), .Cin(alu_1_bit_3_cout), .A_Invert(A_Invert),
    .B_Invert(B_Invert), .Select_Bit_Operation(Operation_Code), .Result(Result[3]));
  ALU_1_bit alu_1_bit_5 (
    .A(Input_A[4]), .B(Input_B[4]), .Cout(alu_1_bit_5_cout), .Cin(alu_1_bit_4_cout), .A_Invert(A_Invert),
    .B_Invert(B_Invert), .Select_Bit_Operation(Operation_Code), .Result(Result[4]));
  ALU_1_bit alu_1_bit_6 (
    .A(Input_A[5]), .B(Input_B[5]), .Cout(alu_1_bit_6_cout), .Cin(alu_1_bit_5_cout), .A_Invert(A_Invert),
    .B_Invert(B_Invert), .Select_Bit_Operation(Operation_Code), .Result(Result[5]));
  ALU_1_bit alu_1_bit_7 (
    .A(Input_A[6]), .B(Input_B[6]), .Cout(alu_1_bit_7_cout), .Cin(alu_1_bit_6_cout), .A_Invert(A_Invert),
    .B_Invert(B_Invert), .Select_Bit_Operation(Operation_Code), .Result(Result[6]));
  ALU_1_bit alu_1_bit_8 (
    .A(Input_A[7]), .B(Input_B[7]), .Cout(alu_1_bit_8_cout), .Cin(alu_1_bit_7_cout), .A_Invert(A_Invert),
    .B_Invert(B_Invert), .Select_Bit_Operation(Operation_Code), .Result(Result[7]));
  ALU_1_bit alu_1_bit_9 (
    .A(Input_A[8]), .B(Input_B[8]), .Cout(alu_1_bit_9_cout), .Cin(alu_1_bit_8_cout), .A_Invert(A_Invert),
    .B_Invert(B_Invert), .Select_Bit_Operation(Operation_Code), .Result(Result[8]));
  ALU_1_bit alu_1_bit_10 (
    .A(Input_A[9]), .B(Input_B[9]), .Cout(alu_1_bit_10_cout), .Cin(alu_1_bit_9_cout), .A_Invert(A_Invert),
    .B_Invert(B_Invert), .Select_Bit_Operation(Operation_Code), .Result(Result[9]));
  ALU_1_bit alu_1_bit_11 (
    .A(Input_A[10]), .B(Input_B[10]), .Cout(alu_1_bit_11_cout), .Cin(alu_1_bit_10_cout), .A_Invert(A_Invert),
    .B_Invert(B_Invert), .Select_Bit_Operation(Operation_Code), .Result(Result[10]));
  ALU_1_bit alu_1_bit_12 (
    .A(Input_A[11]), .B(Input_B[11]), .Cout(alu_1_bit_12_cout), .Cin(alu_1_bit_11_cout), .A_Invert(A_Invert),
    .B_Invert(B_Invert), .Select_Bit_Operation(Operation_Code), .Result(Result[11]));
  ALU_1_bit alu_1_bit_13 (
    .A(Input_A[12]), .B(Input_B[12]), .Cout(alu_1_bit_13_cout), .Cin(alu_1_bit_12_cout), .A_Invert(A_Invert),
    .B_Invert(B_Invert), .Select_Bit_Operation(Operation_Code), .Result(Result[12]));
  ALU_1_bit alu_1_bit_14 (
    .A(Input_A[13]), .B(Input_B[13]), .Cout(alu_1_bit_14_cout), .Cin(alu_1_bit_13_cout), .A_Invert(A_Invert),
    .B_Invert(B_Invert), .Select_Bit_Operation(Operation_Code), .Result(Result[13]));
  ALU_1_bit alu_1_bit_15 (
    .A(Input_A[14]), .B(Input_B[14]), .Cout(alu_1_bit_15_cout), .Cin(alu_1_bit_14_cout), .A_Invert(A_Invert),
    .B_Invert(B_Invert), .Select_Bit_Operation(Operation_Code), .Result(Result[14]));
  ALU_1_bit alu_1_bit_16 (
    .A(Input_A[15]), .B(Input_B[15]), .Cout(alu_1_bit_16_cout), .Cin(alu_1_bit_15_cout), .A_Invert(A_Invert),
    .B_Invert(B_Invert), .Select_Bit_Operation(Operation_Code), .Result(Result[15]));
  nor nor_1 (Zero_Flag, Result[0], Result[1], Result[2], Result[3], Result[4], Result[5], Result[6], Result[7], Result[8], Result[9], Result[10], Result[11], Result[12], Result[13], Result[14], Result[15]);
  xor xor_1 (OverFlow, alu_1_bit_15_cout, alu_1_bit_16_cout);

  // Notes on the sheet:
  //   AbdullahMahmood
  //   ALU 16 BIT
endmodule

// 1 Bit ALU
module ALU_1_bit (
  input  Cin,
  input  A,
  input  A_Invert,
  input  B,
  input  B_Invert,
  input  [1:0] Select_Bit_Operation,
  output Result,
  output Cout
);

  wire adder_1_out, AND_out, multiplexer_1_out, multiplexer_2_out, not_1_out, not_2_out, OR_out, xor_out;

  Multiplexer multiplexer_1 (.in0(A), .in1(not_1_out), .out(multiplexer_1_out), .sel(A_Invert));  // open: en
  not not_1 (not_1_out, A);
  not not_2 (not_2_out, B);
  Multiplexer multiplexer_2 (.in0(B), .in1(not_2_out), .out(multiplexer_2_out), .sel(B_Invert));  // open: en
  and AND (AND_out, multiplexer_1_out, multiplexer_2_out);
  or OR (OR_out, multiplexer_1_out, multiplexer_2_out);
  xor \xor  (xor_out, multiplexer_1_out, multiplexer_2_out);
  Adder #(.width(1)) adder_1 (.a(multiplexer_1_out), .b(multiplexer_2_out), .out(adder_1_out), .cin(Cin), .cout(Cout));
  Multiplexer #(.select(2)) multiplexer_3 (
    .in0(AND_out), .in1(OR_out), .in2(xor_out), .in3(adder_1_out), .out(Result), .sel(Select_Bit_Operation));  // open: en

  // Notes on the sheet:
  //   AbdullahMahmood
  //   ALU 1BIT
endmodule

module Forward_Unit (
  input  EX_MEM_RegWrite,
  input  [3:0] EX_MEM_RegisterRd,
  input  [3:0] ID_EX_Rs,
  input  [3:0] ID_EX_Rt,
  input  [3:0] MEM_WB_RegisterRd,
  input  MEM_WB_RegWrite,
  output [1:0] ForwardMUXA,
  output [1:0] ForwardMUXB
);

  wire comparator_1_eq, comparator_2_eq, comparator_3_eq, comparator_4_eq, FA0_2_out, FA1_2_out, FB0_2_out,
       FB1_2_out;
  wire [3:0] and_1_out, and_2_out, bit_extender_1_out, bit_extender_2_out, bit_extender_3_out,
       bit_extender_4_out, bit_extender_5_out, bit_extender_6_out, FA0_out, FA1_out, FB0_out, FB1_out;

  assign bit_extender_1_out = {{3{EX_MEM_RegWrite}}, EX_MEM_RegWrite};  // Bit_Extender bit_extender_1
  assign bit_extender_2_out = {{3{MEM_WB_RegWrite}}, MEM_WB_RegWrite};  // Bit_Extender bit_extender_2
  assign and_1_out = bit_extender_1_out & EX_MEM_RegisterRd;  // AND_Gate and_1, 4 bits wide
  Comparator #(.width(4)) comparator_1 (.a(EX_MEM_RegisterRd), .b(ID_EX_Rs), .eq(comparator_1_eq));  // open: gt, lt
  Comparator #(.width(4)) comparator_2 (.a(EX_MEM_RegisterRd), .b(ID_EX_Rt), .eq(comparator_2_eq));  // open: gt, lt
  Comparator #(.width(4)) comparator_3 (.a(ID_EX_Rs), .b(MEM_WB_RegisterRd), .eq(comparator_3_eq));  // open: gt, lt
  Comparator #(.width(4)) comparator_4 (.a(ID_EX_Rt), .b(MEM_WB_RegisterRd), .eq(comparator_4_eq));  // open: gt, lt
  assign and_2_out = MEM_WB_RegisterRd & bit_extender_2_out;  // AND_Gate and_2, 4 bits wide
  assign bit_extender_3_out = {{3{comparator_1_eq}}, comparator_1_eq};  // Bit_Extender bit_extender_3
  assign bit_extender_4_out = {{3{comparator_2_eq}}, comparator_2_eq};  // Bit_Extender bit_extender_4
  assign bit_extender_5_out = {{3{comparator_3_eq}}, comparator_3_eq};  // Bit_Extender bit_extender_5
  assign bit_extender_6_out = {{3{comparator_4_eq}}, comparator_4_eq};  // Bit_Extender bit_extender_6
  assign FA1_out = and_1_out & bit_extender_3_out;  // AND_Gate FA1, 4 bits wide
  assign FB1_out = and_1_out & bit_extender_4_out;  // AND_Gate FB1, 4 bits wide
  assign FA0_out = bit_extender_5_out & and_2_out;  // AND_Gate FA0, 4 bits wide
  assign FB0_out = bit_extender_6_out & and_2_out;  // AND_Gate FB0, 4 bits wide
  and FA0_2 (FA0_2_out, ~FA0_out[0], ~FA0_out[1], ~FA0_out[2], ~FA0_out[3]);  // AND_Gate
  and FA1_2 (FA1_2_out, ~FA1_out[0], ~FA1_out[1], ~FA1_out[2], ~FA1_out[3]);  // AND_Gate
  and FB0_2 (FB0_2_out, ~FB0_out[0], ~FB0_out[1], ~FB0_out[2], ~FB0_out[3]);  // AND_Gate
  and FB1_2 (FB1_2_out, ~FB1_out[0], ~FB1_out[1], ~FB1_out[2], ~FB1_out[3]);  // AND_Gate
  not not_1 (ForwardMUXA[0], FA0_2_out);
  not not_2 (ForwardMUXA[1], FA1_2_out);
  not not_3 (ForwardMUXB[0], FB0_2_out);
  not not_4 (ForwardMUXB[1], FB1_2_out);
endmodule

module Hazard_Detection_Unit (
  input  [3:0] IF___ID_RegisterRs,
  input  [3:0] ID___EX_RegisterRt,
  input  [3:0] IF___ID_RegisterRt,
  input  ID___EX_MemRead,
  output FlushControl,
  output PCWrite,
  output IF___ID_Write
);

  wire comparator_1_eq, comparator_2_eq, or_1_out;

  Comparator #(.width(4)) comparator_1 (
    .a(IF___ID_RegisterRs), .b(ID___EX_RegisterRt), .eq(comparator_1_eq));  // open: gt, lt
  Comparator #(.width(4)) comparator_2 (
    .a(ID___EX_RegisterRt), .b(IF___ID_RegisterRt), .eq(comparator_2_eq));  // open: gt, lt
  or or_1 (or_1_out, comparator_1_eq, comparator_2_eq);
  and and_1 (FlushControl, or_1_out, ID___EX_MemRead);
  not not_1 (IF___ID_Write, FlushControl);

  assign PCWrite = IF___ID_Write;
endmodule
