// Logisim project Pipeline Datapath.circ as structural Verilog: 6 circuits, main circuit DataPath
// CPU :)
module DataPath (
  output [1:0] out_1,
  output [3:0] OP,
  output [3:0] RD,
  output [3:0] RS,
  output [3:0] RT,
  output [15:0] out_6,
  output [15:0] out_7,
  output [15:0] Result_Out,
  output [15:0] Data1_Out,
  output [15:0] Data2_Out,
  output [15:0] out_11,
  output Overflow,
  output [15:0] out_13,
  output [15:0] out_14,
  output [15:0] out_15,
  output [15:0] out_16,
  output [3:0] out_17,
  output [3:0] out_18,
  output [3:0] out_19,
  output [3:0] out_20
);

  wire alu_16_bit_1_overflow, alu_16_bit_1_zero_flag, branchcircuit_1_output_to_mux, CLOCK_out,
       maincontrolunit_1_a_invert, maincontrolunit_1_alusrc, maincontrolunit_1_beq_bne_line,
       maincontrolunit_1_binvert, maincontrolunit_1_branch, maincontrolunit_1_memread,
       maincontrolunit_1_memtoreg, maincontrolunit_1_memwrite, maincontrolunit_1_regdst,
       maincontrolunit_1_regwrite, register_3_q, register_4_q, register_5_q, register_6_q, register_7_q,
       register_8_q, register_9_q, register_10_q, register_12_q, register_18_q, register_19_q, register_20_q,
       register_21_q, register_22_q, register_23_q, register_25_q, register_27_q, register_30_q,
       register_31_q;
  wire [1:0] maincontrolunit_1_aluop;
  wire [3:0] register_2_q;
  wire [15:0] adder_1_out, adder_2_out, multiplexer_1_out, multiplexer_3_out, PC_q, ram_1_data, register_1_q,
       register_13_q, register_24_q, register_32_q, register_33_q, rom_1_data, shifter_1_out;

  Multiplexer #(.width(16), .enable("false")) multiplexer_1 (
    .in0(adder_1_out), .in1(register_24_q), .out(multiplexer_1_out), .sel(branchcircuit_1_output_to_mux));
  Register #(.width(16)) PC (.D(multiplexer_1_out), .Q(PC_q), .clk(CLOCK_out));  // open: en, clr
  Button CLOCK (.out(CLOCK_out));
  Adder #(.width(16)) adder_1 (.a(16'h1), .b(PC_q), .out(adder_1_out));  // open: cin, cout
  ROM #(.addrWidth(16), .dataWidth(16)) rom_1 (.addr(PC_q), .data(rom_1_data));  // open: sel
  Register #(.width(16)) register_1 (.D(adder_1_out), .Q(register_1_q), .clk(CLOCK_out));  // open: en, clr
  Register #(.width(16)) register_2 (
    .D(rom_1_data), .Q({OP, out_17, RS, register_2_q}), .clk(CLOCK_out));  // open: en, clr
  MainControlUnit maincontrolunit_1 (
    .Ins_Input(OP), .RegWrite(maincontrolunit_1_regwrite), .ALUsrc(maincontrolunit_1_alusrc),
    .Binvert(maincontrolunit_1_binvert), .A_invert(maincontrolunit_1_a_invert),
    .MemToReg(maincontrolunit_1_memtoreg), .MemRead(maincontrolunit_1_memread),
    .MemWrite(maincontrolunit_1_memwrite), .Branch(maincontrolunit_1_branch),
    .ALUop(maincontrolunit_1_aluop), .BEQ_BNE_Line(maincontrolunit_1_beq_bne_line),
    .REGDst(maincontrolunit_1_regdst));
  Multiplexer #(.width(4), .enable("false")) multiplexer_2 (
    .in0(register_2_q), .in1(out_17), .out(RT), .sel(maincontrolunit_1_regdst));
  RegisterFile registerfile_1 (
    .Write_Data_IN(Result_Out), .Data01(Data1_Out), .Data02(Data2_Out), .RD(out_20), .RS(RS), .RT(RT),
    .Clock(CLOCK_out), .RegWrite(register_30_q));
  assign out_13 = {{12{register_2_q[3]}}, register_2_q};  // Bit_Extender bit_extender_1
  Register #(.width(1)) register_3 (
    .D(maincontrolunit_1_beq_bne_line), .Q(register_3_q), .clk(CLOCK_out));  // open: en, clr
  Register #(.width(1)) register_4 (
    .D(maincontrolunit_1_regwrite), .Q(register_4_q), .clk(CLOCK_out));  // open: en, clr
  Register #(.width(1)) register_5 (
    .D(maincontrolunit_1_memtoreg), .Q(register_5_q), .clk(CLOCK_out));  // open: en, clr
  Register #(.width(1)) register_6 (.D(maincontrolunit_1_memread), .Q(register_6_q), .clk(CLOCK_out));  // open: en, clr
  Register #(.width(1)) register_7 (
    .D(maincontrolunit_1_memwrite), .Q(register_7_q), .clk(CLOCK_out));  // open: en, clr
  Register #(.width(1)) register_8 (.D(maincontrolunit_1_branch), .Q(register_8_q), .clk(CLOCK_out));  // open: en, clr
  Register #(.width(1)) register_9 (.D(maincontrolunit_1_binvert), .Q(register_9_q), .clk(CLOCK_out));  // open: en, clr
  Register #(.width(1)) register_10 (
    .D(maincontrolunit_1_a_invert), .Q(register_10_q), .clk(CLOCK_out));  // open: en, clr
  Register #(.width(2)) register_11 (.D(maincontrolunit_1_aluop), .Q(out_1), .clk(CLOCK_out));  // open: en, clr
  Register #(.width(1)) register_12 (
    .D(maincontrolunit_1_alusrc), .Q(register_12_q), .clk(CLOCK_out));  // open: en, clr
  Register #(.width(16)) register_13 (.D(register_1_q), .Q(register_13_q), .clk(CLOCK_out));  // open: en, clr
  Register #(.width(16)) register_14 (.D(Data1_Out), .Q(out_11), .clk(CLOCK_out));  // open: en, clr
  Register #(.width(16)) register_15 (.D(Data2_Out), .Q(out_15), .clk(CLOCK_out));  // open: en, clr
  Register #(.width(16)) register_16 (.D(out_13), .Q(out_14), .clk(CLOCK_out));  // open: en, clr
  Register #(.width(4)) register_17 (.D(out_17), .Q(out_18), .clk(CLOCK_out));  // open: en, clr
  Multiplexer #(.width(16), .enable("false")) multiplexer_3 (
    .in0(out_15), .in1(out_14), .out(multiplexer_3_out), .sel(register_12_q));
  Shifter #(.width(16)) shifter_1 (.in(out_14), .\dist (4'b0001), .out(shifter_1_out));
  ALU_16_bit alu_16_bit_1 (
    .B_Invert(register_9_q), .A_Invert(register_10_q), .Zero_Flag(alu_16_bit_1_zero_flag),
    .Input_B(multiplexer_3_out), .Input_A(out_11), .Operation_Code(out_1), .OverFlow(alu_16_bit_1_overflow),
    .Result(out_6), .Cin(register_9_q));
  Adder #(.width(16)) adder_2 (.a(register_13_q), .b(shifter_1_out), .out(adder_2_out));  // open: cin, cout
  Register #(.width(1)) register_18 (.D(register_3_q), .Q(register_18_q), .clk(CLOCK_out));  // open: en, clr
  Register #(.width(1)) register_19 (.D(register_4_q), .Q(register_19_q), .clk(CLOCK_out));  // open: en, clr
  Register #(.width(1)) register_20 (.D(register_5_q), .Q(register_20_q), .clk(CLOCK_out));  // open: en, clr
  Register #(.width(1)) register_21 (.D(register_6_q), .Q(register_21_q), .clk(CLOCK_out));  // open: en, clr
  Register #(.width(1)) register_22 (.D(register_7_q), .Q(register_22_q), .clk(CLOCK_out));  // open: en, clr
  Register #(.width(1)) register_23 (.D(register_8_q), .Q(register_23_q), .clk(CLOCK_out));  // open: en, clr
  Register #(.width(16)) register_24 (.D(adder_2_out), .Q(register_24_q), .clk(CLOCK_out));  // open: en, clr
  Register #(.width(1)) register_25 (.D(alu_16_bit_1_zero_flag), .Q(register_25_q), .clk(CLOCK_out));  // open: en, clr
  Register #(.width(16)) register_26 (.D(out_6), .Q(out_7), .clk(CLOCK_out));  // open: en, clr
  Register #(.width(1)) register_27 (.D(alu_16_bit_1_overflow), .Q(register_27_q), .clk(CLOCK_out));  // open: en, clr
  Register #(.width(16)) register_28 (.D(out_15), .Q(out_16), .clk(CLOCK_out));  // open: en, clr
  Register #(.width(4)) register_29 (.D(out_18), .Q(out_19), .clk(CLOCK_out));  // open: en, clr
  BranchCircuit branchcircuit_1 (
    .Output_to_MUX(branchcircuit_1_output_to_mux), .Beq_Bne_CU_Line_In(register_18_q),
    .Branch_CU_Line_In(register_23_q), .ALU_Zero_Flag_IN(register_25_q));
  RAM #(.addrWidth(16), .dataWidth(16), .bus("separate")) ram_1 (
    .addr(out_7), .din(out_16), .data(ram_1_data), .str(register_22_q), .clk(CLOCK_out), .ld(register_21_q));  // open: sel, clr
  Register #(.width(1)) register_30 (.D(register_19_q), .Q(register_30_q), .clk(CLOCK_out));  // open: en, clr
  Register #(.width(1)) register_31 (.D(register_20_q), .Q(register_31_q), .clk(CLOCK_out));  // open: en, clr
  Register #(.width(16)) register_32 (.D(out_7), .Q(register_32_q), .clk(CLOCK_out));  // open: en, clr
  Register #(.width(16)) register_33 (.D(ram_1_data), .Q(register_33_q), .clk(CLOCK_out));  // open: en, clr
  Register #(.width(1)) register_34 (.D(register_27_q), .Q(Overflow), .clk(CLOCK_out));  // open: en, clr
  Register #(.width(4)) register_35 (.D(out_19), .Q(out_20), .clk(CLOCK_out));  // open: en, clr
  Multiplexer #(.width(16), .enable("false")) multiplexer_4 (
    .in0(register_32_q), .in1(register_33_q), .out(Result_Out), .sel(register_31_q));

  assign RD = out_20;

  // Notes on the sheet:
  //   contents of rom_1 (hex, n*v repeats v):
  //   8113 0 0 0 211 0 0 0 1221 0 0 0 8324 0 0 0 2413 0 0 0 3421 0 0 0 8447 0 0 0 4534 0 0 0 5545 0 0 0
  //   6645 0 0 0 b657 0 0 0 c56d 0 0 0 d953 0 0 0 1169 0 0 0 1265 0 0 0 a124 0 0 0 9324 0 0 0 8436 0 0 0
  //   a426 0 0 0 9526 0 0 0 9626 0 0 0 756 0 0 0 e671 0 0 0 e561
  //   IF/ID 32Bits
  //   ID/EX 79Bits
  //   Pipeline Datapath
  //   EX/MEM 60Bits
  //   MEM/WB 39Bits
  //   AbiMahmood
endmodule

module MainControlUnit (
  input  [3:0] Ins_Input,
  output RegWrite,
  output ALUsrc,
  output Binvert,
  output A_invert,
  output MemToReg,
  output MemRead,
  output MemWrite,
  output Branch,
  output REGDst,
  output [1:0] ALUop,
  output BEQ_BNE_Line
);

  wire ADD_0000_out, ADDi_1000_out, AND_0100_out, ANDi_1100_out, BNE_1111_out, NAND_0110_out, noOp_out,
       Nor_0010_out, OR_0011_out, ORi_1011_out, Sub_0001_out, XOR_0101_out, XORi_1101_out;

  and ADD_0000 (ADD_0000_out, ~Ins_Input[3], ~Ins_Input[2], ~Ins_Input[1], ~Ins_Input[0]);  // AND_Gate
  and Sub_0001 (Sub_0001_out, ~Ins_Input[3], ~Ins_Input[2], ~Ins_Input[1], Ins_Input[0]);  // AND_Gate
  and Nor_0010 (Nor_0010_out, ~Ins_Input[3], ~Ins_Input[2], Ins_Input[1], ~Ins_Input[0]);  // AND_Gate
  and OR_0011 (OR_0011_out, ~Ins_Input[3], ~Ins_Input[2], Ins_Input[1], Ins_Input[0]);  // AND_Gate
  and AND_0100 (AND_0100_out, ~Ins_Input[3], Ins_Input[2], ~Ins_Input[1], ~Ins_Input[0]);  // AND_Gate
  and XOR_0101 (XOR_0101_out, ~Ins_Input[3], Ins_Input[2], ~Ins_Input[1], Ins_Input[0]);  // AND_Gate
  and NAND_0110 (NAND_0110_out, ~Ins_Input[3], Ins_Input[2], Ins_Input[1], ~Ins_Input[0]);  // AND_Gate
  and noOp (noOp_out, ~Ins_Input[3], Ins_Input[2], Ins_Input[1], Ins_Input[0]);  // AND_Gate
  and ADDi_1000 (ADDi_1000_out, Ins_Input[3], ~Ins_Input[2], ~Ins_Input[1], ~Ins_Input[0]);  // AND_Gate
  and lw_1001 (MemRead, Ins_Input[3], ~Ins_Input[2], ~Ins_Input[1], Ins_Input[0]);  // AND_Gate
  and sw_1010 (MemWrite, Ins_Input[3], ~Ins_Input[2], Ins_Input[1], ~Ins_Input[0]);  // AND_Gate
  and ORi_1011 (ORi_1011_out, Ins_Input[3], ~Ins_Input[2], Ins_Input[1], Ins_Input[0]);  // AND_Gate
  and ANDi_1100 (ANDi_1100_out, Ins_Input[3], Ins_Input[2], ~Ins_Input[1], ~Ins_Input[0]);  // AND_Gate
  and XORi_1101 (XORi_1101_out, Ins_Input[3], Ins_Input[2], ~Ins_Input[1], Ins_Input[0]);  // AND_Gate
  and BEQ_1110 (Branch, Ins_Input[3], Ins_Input[2], Ins_Input[1], ~Ins_Input[0]);  // AND_Gate
  and BNE_1111 (BNE_1111_out, Ins_Input[3], Ins_Input[2], Ins_Input[1], Ins_Input[0]);
  or or_1 (RegWrite, ADD_0000_out, Sub_0001_out, Nor_0010_out, OR_0011_out, AND_0100_out, XOR_0101_out, NAND_0110_out, noOp_out, ADDi_1000_out, MemRead, ORi_1011_out, ANDi_1100_out, XORi_1101_out);
  or or_2 (ALUsrc, noOp_out, ADDi_1000_out, MemRead, MemWrite, ORi_1011_out, ANDi_1100_out, XORi_1101_out);
  or or_3 (Binvert, NAND_0110_out, Sub_0001_out, Nor_0010_out, noOp_out, Branch, BNE_1111_out);
  or or_4 (A_invert, NAND_0110_out, Nor_0010_out);
  or or_5 (REGDst, Branch, MemWrite, BNE_1111_out);
  or _1st (ALUop[1], ADD_0000_out, Sub_0001_out, XOR_0101_out, noOp_out, ADDi_1000_out, MemRead, MemWrite, XORi_1101_out, Branch, BNE_1111_out);
  or _2nd (ALUop[0], ADD_0000_out, Sub_0001_out, OR_0011_out, noOp_out, ADDi_1000_out, NAND_0110_out, MemRead, MemWrite, ORi_1011_out, Branch, BNE_1111_out);
  or or_6 (BEQ_BNE_Line, BNE_1111_out, Branch);

  assign MemToReg = MemRead;

  // Notes on the sheet:
  //   AbdullahMahmood
  //   0     1     2      3     4       5      6      7      8     9     10     11    12    13     14    15  
  //   Main Control Unit
endmodule

module BranchCircuit (
  input  Beq_Bne_CU_Line_In,
  input  Branch_CU_Line_In,
  input  ALU_Zero_Flag_IN,
  output Output_to_MUX
);

  wire not_1_out, xor_1_out;

  and and_1 (Output_to_MUX, Beq_Bne_CU_Line_In, not_1_out);
  not not_1 (not_1_out, xor_1_out);
  xor xor_1 (xor_1_out, Branch_CU_Line_In, ALU_Zero_Flag_IN);

  // Notes on the sheet:
  //   Branch Circuit
  //   Instructions    Branch    ALUZ    BCU   Output    invert
  //   BNE                    0             0        1         1            0
  //   BNE                    0             1        1         0            1
  //   BEQ                    1             0        1         0            1
  //   BEQ                    1             1        1         1            0
  //   Other ins             0             0        0         0
  //   Other ins             0             1        0         0
  //   Truth Table 
  //   AND Gate
  //   Xor + Not Gate
  //   AbdullahMahmood
endmodule

// Registers
module RegisterFile (
  input  Clock,
  input  [15:0] Write_Data_IN,
  input  RegWrite,
  input  [3:0] RS,
  input  [3:0] RD,
  input  [3:0] RT,
  output [15:0] Data01,
  output [15:0] Data02
);

  wire and_1_out, and_2_out, and_3_out, and_4_out, and_5_out, and_6_out, and_7_out, and_8_out, and_9_out,
       and_10_out, and_11_out, and_12_out, and_13_out, and_14_out, and_15_out, and_16_out, decoder_1_out0,
       decoder_1_out1, decoder_1_out2, decoder_1_out3, decoder_1_out4, decoder_1_out5, decoder_1_out6,
       decoder_1_out7, decoder_1_out8, decoder_1_out9, decoder_1_out10, decoder_1_out11, decoder_1_out12,
       decoder_1_out13, decoder_1_out14, decoder_1_out15;
  wire [15:0] register_1_q, register_2_q, register_3_q, register_4_q, register_5_q, register_6_q,
       register_7_q, register_8_q, register_9_q, register_10_q, register_11_q, register_12_q, register_13_q,
       register_14_q, register_15_q, register_16_q;

  Decoder #(.select(4)) decoder_1 (
    .out0(decoder_1_out0), .out1(decoder_1_out1), .out2(decoder_1_out2), .out3(decoder_1_out3),
    .out4(decoder_1_out4), .out5(decoder_1_out5), .out6(decoder_1_out6), .out7(decoder_1_out7),
    .out8(decoder_1_out8), .out9(decoder_1_out9), .out10(decoder_1_out10), .out11(decoder_1_out11),
    .out12(decoder_1_out12), .out13(decoder_1_out13), .out14(decoder_1_out14), .out15(decoder_1_out15),
    .sel(RD));  // open: en
  and and_1 (and_1_out, RegWrite, decoder_1_out0);
  and and_2 (and_2_out, RegWrite, decoder_1_out1);
  and and_3 (and_3_out, RegWrite, decoder_1_out2);
  and and_4 (and_4_out, RegWrite, decoder_1_out3);
  and and_5 (and_5_out, RegWrite, decoder_1_out4);
  and and_6 (and_6_out, RegWrite, decoder_1_out5);
  and and_7 (and_7_out, RegWrite, decoder_1_out6);
  and and_8 (and_8_out, RegWrite, decoder_1_out7);
  and and_9 (and_9_out, RegWrite, decoder_1_out8);
  and and_10 (and_10_out, RegWrite, decoder_1_out9);
  and and_11 (and_11_out, RegWrite, decoder_1_out10);
  and and_12 (and_12_out, RegWrite, decoder_1_out11);
  and and_13 (and_13_out, RegWrite, decoder_1_out12);
  and and_14 (and_14_out, RegWrite, decoder_1_out13);
  and and_15 (and_15_out, RegWrite, decoder_1_out14);
  and and_16 (and_16_out, RegWrite, decoder_1_out15);
  Register #(.width(16)) register_1 (.D(Write_Data_IN), .en(and_1_out), .Q(register_1_q), .clk(Clock));  // open: clr
  Register #(.width(16)) register_2 (.D(Write_Data_IN), .en(and_2_out), .Q(register_2_q), .clk(Clock));  // open: clr
  Register #(.width(16)) register_3 (.D(Write_Data_IN), .en(and_3_out), .Q(register_3_q), .clk(Clock));  // open: clr
  Register #(.width(16)) register_4 (.D(Write_Data_IN), .en(and_4_out), .Q(register_4_q), .clk(Clock));  // open: clr
  Register #(.width(16)) register_5 (.D(Write_Data_IN), .en(and_5_out), .Q(register_5_q), .clk(Clock));  // open: clr
  Register #(.width(16)) register_6 (.D(Write_Data_IN), .en(and_6_out), .Q(register_6_q), .clk(Clock));  // open: clr
  Register #(.width(16)) register_7 (.D(Write_Data_IN), .en(and_7_out), .Q(register_7_q), .clk(Clock));  // open: clr
  Register #(.width(16)) register_8 (.D(Write_Data_IN), .en(and_8_out), .Q(register_8_q), .clk(Clock));  // open: clr
  Register #(.width(16)) register_9 (.D(Write_Data_IN), .en(and_9_out), .Q(register_9_q), .clk(Clock));  // open: clr
  Register #(.width(16)) register_10 (.D(Write_Data_IN), .en(and_10_out), .Q(register_10_q), .clk(Clock));  // open: clr
  Register #(.width(16)) register_11 (.D(Write_Data_IN), .en(and_11_out), .Q(register_11_q), .clk(Clock));  // open: clr
  Register #(.width(16)) register_12 (.D(Write_Data_IN), .en(and_12_out), .Q(register_12_q), .clk(Clock));  // open: clr
  Register #(.width(16)) register_13 (.D(Write_Data_IN), .en(and_13_out), .Q(register_13_q), .clk(Clock));  // open: clr
  Register #(.width(16)) register_14 (.D(Write_Data_IN), .en(and_14_out), .Q(register_14_q), .clk(Clock));  // open: clr
  Register #(.width(16)) register_15 (.D(Write_Data_IN), .en(and_15_out), .Q(register_15_q), .clk(Clock));  // open: clr
  Register #(.width(16)) register_16 (.D(Write_Data_IN), .en(and_16_out), .Q(register_16_q), .clk(Clock));  // open: clr
  Multiplexer #(.select(4), .width(16)) multiplexer_1 (
    .in0(register_1_q), .in1(register_2_q), .in2(register_3_q), .in3(register_4_q), .in4(register_5_q),
    .in5(register_6_q), .in6(register_7_q), .in7(register_8_q), .in8(register_9_q), .in9(register_10_q),
    .in10(register_11_q), .in11(register_12_q), .in12(register_13_q), .in13(register_14_q),
    .in14(register_15_q), .in15(register_16_q), .out(Data01), .sel(RS));  // open: en
  Multiplexer #(.select(4), .width(16)) multiplexer_2 (
    .in0(register_1_q), .in1(register_2_q), .in2(register_3_q), .in3(register_4_q), .in4(register_5_q),
    .in5(register_6_q), .in6(register_7_q), .in7(register_8_q), .in8(register_9_q), .in9(register_10_q),
    .in10(register_11_q), .in11(register_12_q), .in12(register_13_q), .in13(register_14_q),
    .in14(register_15_q), .in15(register_16_q), .out(Data02), .sel(RT));  // open: en

  // Notes on the sheet:
  //   AbdullahMahmood
  //   Register Files
endmodule

module ALU_16_bit (
  input  Cin,
  input  B_Invert,
  input  A_Invert,
  input  [1:0] Operation_Code,
  input  [15:0] Input_B,
  input  [15:0] Input_A,
  output [15:0] Result,
  output Zero_Flag,
  output OverFlow
);

  wire alu_1_bit_1_cout, alu_1_bit_2_cout, alu_1_bit_3_cout, alu_1_bit_4_cout, alu_1_bit_5_cout,
       alu_1_bit_6_cout, alu_1_bit_7_cout, alu_1_bit_8_cout, alu_1_bit_9_cout, alu_1_bit_10_cout,
       alu_1_bit_11_cout, alu_1_bit_12_cout, alu_1_bit_13_cout, alu_1_bit_14_cout, alu_1_bit_15_cout,
       alu_1_bit_16_cout;

  ALU_1_bit alu_1_bit_1 (
    .A(Input_A[0]), .B(Input_B[0]), .Cout(alu_1_bit_1_cout), .Cin(Cin), .A_Invert(A_Invert),
    .B_Invert(B_Invert), .Select_Bit_Operation(Operation_Code), .Result(Result[0]));
  ALU_1_bit alu_1_bit_2 (
    .A(Input_A[1]), .B(Input_B[1]), .Cout(alu_1_bit_2_cout), .Cin(alu_1_bit_1_cout), .A_Invert(A_Invert),
    .B_Invert(B_Invert), .Select_Bit_Operation(Operation_Code), .Result(Result[1]));
  ALU_1_bit alu_1_bit_3 (
    .A(Input_A[2]), .B(Input_B[2]), .Cout(alu_1_bit_3_cout), .Cin(alu_1_bit_2_cout), .A_Invert(A_Invert),
    .B_Invert(B_Invert), .Select_Bit_Operation(Operation_Code), .Result(Result[2]));
  ALU_1_bit alu_1_bit_4 (
    .A(Input_A[3]), .B(Input_B[3]), .Cout(alu_1_bit_4_cout), .Cin(alu_1_bit_3_cout), .A_Invert(A_Invert),
    .B_Invert(B_Invert), .Select_Bit_Operation(Operation_Code), .Result(Result[3]));
  ALU_1_bit alu_1_bit_5 (
    .A(Input_A[4]), .B(Input_B[4]), .Cout(alu_1_bit_5_cout), .Cin(alu_1_bit_4_cout), .A_Invert(A_Invert),
    .B_Invert(B_Invert), .Select_Bit_Operation(Operation_Code), .Result(Result[4]));
  ALU_1_bit alu_1_bit_6 (
    .A(Input_A[5]), .B(Input_B[5]), .Cout(alu_1_bit_6_cout), .Cin(alu_1_bit_5_cout), .A_Invert(A_Invert),
    .B_Invert(B_Invert), .Select_Bit_Operation(Operation_Code), .Result(Result[5]));
  ALU_1_bit alu_1_bit_7 (
    .A(Input_A[6]), .B(Input_B[6]), .Cout(alu_1_bit_7_cout), .Cin(alu_1_bit_6_cout), .A_Invert(A_Invert),
    .B_Invert(B_Invert), .Select_Bit_Operation(Operation_Code), .Result(Result[6]));
  ALU_1_bit alu_1_bit_8 (
    .A(Input_A[7]), .B(Input_B[7]), .Cout(alu_1_bit_8_cout), .Cin(alu_1_bit_7_cout), .A_Invert(A_Invert),
    .B_Invert(B_Invert), .Select_Bit_Operation(Operation_Code), .Result(Result[7]));
  ALU_1_bit alu_1_bit_9 (
    .A(Input_A[8]), .B(Input_B[8]), .Cout(alu_1_bit_9_cout), .Cin(alu_1_bit_8_cout), .A_Invert(A_Invert),
    .B_Invert(B_Invert), .Select_Bit_Operation(Operation_Code), .Result(Result[8]));
  ALU_1_bit alu_1_bit_10 (
    .A(Input_A[9]), .B(Input_B[9]), .Cout(alu_1_bit_10_cout), .Cin(alu_1_bit_9_cout), .A_Invert(A_Invert),
    .B_Invert(B_Invert), .Select_Bit_Operation(Operation_Code), .Result(Result[9]));
  ALU_1_bit alu_1_bit_11 (
    .A(Input_A[10]), .B(Input_B[10]), .Cout(alu_1_bit_11_cout), .Cin(alu_1_bit_10_cout), .A_Invert(A_Invert),
    .B_Invert(B_Invert), .Select_Bit_Operation(Operation_Code), .Result(Result[10]));
  ALU_1_bit alu_1_bit_12 (
    .A(Input_A[11]), .B(Input_B[11]), .Cout(alu_1_bit_12_cout), .Cin(alu_1_bit_11_cout), .A_Invert(A_Invert),
    .B_Invert(B_Invert), .Select_Bit_Operation(Operation_Code), .Result(Result[11]));
  ALU_1_bit alu_1_bit_13 (
    .A(Input_A[12]), .B(Input_B[12]), .Cout(alu_1_bit_13_cout), .Cin(alu_1_bit_12_cout), .A_Invert(A_Invert),
    .B_Invert(B_Invert), .Select_Bit_Operation(Operation_Code), .Result(Result[12]));
  ALU_1_bit alu_1_bit_14 (
    .A(Input_A[13]), .B(Input_B[13]), .Cout(alu_1_bit_14_cout), .Cin(alu_1_bit_13_cout), .A_Invert(A_Invert),
    .B_Invert(B_Invert), .Select_Bit_Operation(Operation_Code), .Result(Result[13]));
  ALU_1_bit alu_1_bit_15 (
    .A(Input_A[14]), .B(Input_B[14]), .Cout(alu_1_bit_15_cout), .Cin(alu_1_bit_14_cout), .A_Invert(A_Invert),
    .B_Invert(B_Invert), .Select_Bit_Operation(Operation_Code), .Result(Result[14]));
  ALU_1_bit alu_1_bit_16 (
    .A(Input_A[15]), .B(Input_B[15]), .Cout(alu_1_bit_16_cout), .Cin(alu_1_bit_15_cout), .A_Invert(A_Invert),
    .B_Invert(B_Invert), .Select_Bit_Operation(Operation_Code), .Result(Result[15]));
  nor nor_1 (Zero_Flag, Result[0], Result[1], Result[2], Result[3], Result[4], Result[5], Result[6], Result[7], Result[8], Result[9], Result[10], Result[11], Result[12], Result[13], Result[14], Result[15]);
  xor xor_1 (OverFlow, alu_1_bit_15_cout, alu_1_bit_16_cout);

  // Notes on the sheet:
  //   AbdullahMahmood
  //   ALU 16 BIT
endmodule

// 1 Bit ALU
module ALU_1_bit (
  input  Cin,
  input  A,
  input  A_Invert,
  input  B,
  input  B_Invert,
  input  [1:0] Select_Bit_Operation,
  output Result,
  output Cout
);

  wire adder_1_out, AND_out, multiplexer_1_out, multiplexer_2_out, not_1_out, not_2_out, OR_out, xor_out;

  Multiplexer multiplexer_1 (.in0(A), .in1(not_1_out), .out(multiplexer_1_out), .sel(A_Invert));  // open: en
  not not_1 (not_1_out, A);
  not not_2 (not_2_out, B);
  Multiplexer multiplexer_2 (.in0(B), .in1(not_2_out), .out(multiplexer_2_out), .sel(B_Invert));  // open: en
  and AND (AND_out, multiplexer_1_out, multiplexer_2_out);
  or OR (OR_out, multiplexer_1_out, multiplexer_2_out);
  xor \xor  (xor_out, multiplexer_1_out, multiplexer_2_out);
  Adder #(.width(1)) adder_1 (.a(multiplexer_1_out), .b(multiplexer_2_out), .out(adder_1_out), .cin(Cin), .cout(Cout));
  Multiplexer #(.select(2)) multiplexer_3 (
    .in0(AND_out), .in1(OR_out), .in2(xor_out), .in3(adder_1_out), .out(Result), .sel(Select_Bit_Operation));  // open: en

  // Notes on the sheet:
  //   AbdullahMahmood
  //   ALU 1BIT
endmodule
