// Logisim project SingleCycleDatapath.circ as structural Verilog: 7 circuits, main circuit DataPath
// CPU
module DataPath (
  output [3:0] OP,
  output [3:0] RD,
  output [3:0] RS,
  output [3:0] RT,
  output [15:0] Data1_Out,
  output [15:0] Data2_Out,
  output [15:0] Result_Out,
  output [1:0] ALUopCode
);

  wire alu_16_bit_1_overflow, alu_16_bit_1_zero_flag, branchcircuit_1_output_to_mux, CLOCK_out,
       maincontrolunit_kmap_v2_1_a_invert, maincontrolunit_kmap_v2_1_alusrc,
       maincontrolunit_kmap_v2_1_b_invert, maincontrolunit_kmap_v2_1_beq___bne_line,
       maincontrolunit_kmap_v2_1_branch, maincontrolunit_kmap_v2_1_memread,
       maincontrolunit_kmap_v2_1_memtoreg, maincontrolunit_kmap_v2_1_memwrite,
       maincontrolunit_kmap_v2_1_regdst, maincontrolunit_kmap_v2_1_regwrite;
  wire [3:0] rom_1_data;
  wire [15:0] adder_1_out, adder_2_out, alu_16_bit_1_result, bit_extender_1_out, multiplexer_1_out,
       multiplexer_3_out, PC_q, ram_1_data, shifter_1_out;

  Multiplexer #(.width(16), .enable("false")) multiplexer_1 (
    .in0(adder_1_out), .in1(adder_2_out), .out(multiplexer_1_out), .sel(branchcircuit_1_output_to_mux));
  Register #(.width(16)) PC (.D(multiplexer_1_out), .Q(PC_q), .clk(CLOCK_out));  // open: en, clr
  Button CLOCK (.out(CLOCK_out));
  LED RegDST (.in(maincontrolunit_kmap_v2_1_regdst));
  LED RegWrite (.in(maincontrolunit_kmap_v2_1_regwrite));
  LED ALUsrc (.in(maincontrolunit_kmap_v2_1_alusrc));
  LED A_Invert (.in(maincontrolunit_kmap_v2_1_a_invert));
  LED B_Invert (.in(maincontrolunit_kmap_v2_1_b_invert));
  LED MemWrite (.in(maincontrolunit_kmap_v2_1_memwrite));
  LED MemRead (.in(maincontrolunit_kmap_v2_1_memread));
  LED MemToReg (.in(maincontrolunit_kmap_v2_1_memtoreg));
  LED Branch (.in(maincontrolunit_kmap_v2_1_branch));
  LED BEQ___BNE_Line (.in(maincontrolunit_kmap_v2_1_beq___bne_line));
  LED OverFlow (.in(alu_16_bit_1_overflow));
  MainControlUnit_Kmap_V2 maincontrolunit_kmap_v2_1 (
    .Ins_Input(OP), .A_Invert(maincontrolunit_kmap_v2_1_a_invert),
    .B_Invert(maincontrolunit_kmap_v2_1_b_invert), .RegWrite(maincontrolunit_kmap_v2_1_regwrite),
    .ALUSrc(maincontrolunit_kmap_v2_1_alusrc), .REGdst(maincontrolunit_kmap_v2_1_regdst),
    .MemToReg(maincontrolunit_kmap_v2_1_memtoreg), .MemRead(maincontrolunit_kmap_v2_1_memread),
    .MemWrite(maincontrolunit_kmap_v2_1_memwrite), .Branch(maincontrolunit_kmap_v2_1_branch),
    .BEQ___BNE_Line(maincontrolunit_kmap_v2_1_beq___bne_line), .ALUOp(ALUopCode));
  Adder #(.width(16)) adder_1 (.a(16'h1), .b(PC_q), .out(adder_1_out));  // open: cin, cout
  BranchCircuit branchcircuit_1 (
    .Output_to_MUX(branchcircuit_1_output_to_mux),
    .Beq_Bne_CU_Line_In(maincontrolunit_kmap_v2_1_beq___bne_line), .ALU_Zero_Flag_IN(alu_16_bit_1_zero_flag),
    .Branch_CU_Line_In(maincontrolunit_kmap_v2_1_branch));
  ROM #(.addrWidth(16), .dataWidth(16)) rom_1 (.addr(PC_q), .data({OP, RD, RS, rom_1_data}));  // open: sel
  Multiplexer #(.width(4), .enable("false")) multiplexer_2 (
    .in0(rom_1_data), .in1(RD), .out(RT), .sel(maincontrolunit_kmap_v2_1_regdst));
  RegisterFile registerfile_1 (
    .Write_Data_IN(Result_Out), .Data01(Data1_Out), .Data02(Data2_Out), .RD(RD), .RS(RS), .RT(RT),
    .Clock(CLOCK_out), .RegWrite(maincontrolunit_kmap_v2_1_regwrite));
  assign bit_extender_1_out = {{12{rom_1_data[3]}}, rom_1_data};  // Bit_Extender bit_extender_1
  Multiplexer #(.width(16), .enable("false")) multiplexer_3 (
    .in0(Data2_Out), .in1(bit_extender_1_out), .out(multiplexer_3_out), .sel(maincontrolunit_kmap_v2_1_alusrc));
  Adder #(.width(16)) adder_2 (.a(adder_1_out), .b(shifter_1_out), .out(adder_2_out));  // open: cin, cout
  Shifter #(.width(16)) shifter_1 (.in(bit_extender_1_out), .\dist (4'b0001), .out(shifter_1_out));
  ALU_16_bit alu_16_bit_1 (
    .B_Invert(maincontrolunit_kmap_v2_1_b_invert), .A_Invert(maincontrolunit_kmap_v2_1_a_invert),
    .Zero_Flag(alu_16_bit_1_zero_flag), .Input_B(multiplexer_3_out), .Input_A(Data1_Out),
    .Operation_Code(ALUopCode), .OverFlow(alu_16_bit_1_overflow), .Result(alu_16_bit_1_result),
    .Cin(maincontrolunit_kmap_v2_1_b_invert));
  RAM #(.addrWidth(16), .dataWidth(16), .bus("separate")) ram_1 (
    .addr(alu_16_bit_1_result), .din(Data2_Out), .data(ram_1_data), .str(maincontrolunit_kmap_v2_1_memwrite),
    .clk(CLOCK_out), .ld(maincontrolunit_kmap_v2_1_memread));  // open: sel, clr
  Multiplexer #(.width(16), .enable("false")) multiplexer_4 (
    .in0(alu_16_bit_1_result), .in1(ram_1_data), .out(Result_Out), .sel(maincontrolunit_kmap_v2_1_memtoreg));

  // Notes on the sheet:
  //   contents of rom_1 (hex, n*v repeats v):
  //   1000 9100 9204 9307 1444 424 e502 212 e00b 212 e00b a400 e00f
  //   Single Cycle Datapath
  //   R Type [OP      RD     RS   RT ] 
  //   I Type [OP      RD     RS   imm ] 
  //   (15:12) (11:8) (7:4) (3:0)  
  //   AbdullahMahmood
endmodule

module RegisterFile (
  input  Clock,
  input  [15:0] Write_Data_IN,
  input  RegWrite,
  input  [3:0] RS,
  input  [3:0] RD,
  input  [3:0] RT,
  output [15:0] Data01,
  output [15:0] Data02
);

  wire and_1_out, and_2_out, and_3_out, and_4_out, and_5_out, and_6_out, and_7_out, and_8_out, and_9_out,
       and_10_out, and_11_out, and_12_out, and_13_out, and_14_out, and_15_out, and_16_out, decoder_1_out0,
       decoder_1_out1, decoder_1_out2, decoder_1_out3, decoder_1_out4, decoder_1_out5, decoder_1_out6,
       decoder_1_out7, decoder_1_out8, decoder_1_out9, decoder_1_out10, decoder_1_out11, decoder_1_out12,
       decoder_1_out13, decoder_1_out14, decoder_1_out15;
  wire [15:0] register_1_q, register_2_q, register_3_q, register_4_q, register_5_q, register_6_q,
       register_7_q, register_8_q, register_9_q, register_10_q, register_11_q, register_12_q, register_13_q,
       register_14_q, register_15_q, register_16_q;

  Decoder #(.select(4)) decoder_1 (
    .out0(decoder_1_out0), .out1(decoder_1_out1), .out2(decoder_1_out2), .out3(decoder_1_out3),
    .out4(decoder_1_out4), .out5(decoder_1_out5), .out6(decoder_1_out6), .out7(decoder_1_out7),
    .out8(decoder_1_out8), .out9(decoder_1_out9), .out10(decoder_1_out10), .out11(decoder_1_out11),
    .out12(decoder_1_out12), .out13(decoder_1_out13), .out14(decoder_1_out14), .out15(decoder_1_out15),
    .sel(RD));  // open: en
  and and_1 (and_1_out, RegWrite, decoder_1_out0);
  and and_2 (and_2_out, RegWrite, decoder_1_out1);
  and and_3 (and_3_out, RegWrite, decoder_1_out2);
  and and_4 (and_4_out, RegWrite, decoder_1_out3);
  and and_5 (and_5_out, RegWrite, decoder_1_out4);
  and and_6 (and_6_out, RegWrite, decoder_1_out5);
  and and_7 (and_7_out, RegWrite, decoder_1_out6);
  and and_8 (and_8_out, RegWrite, decoder_1_out7);
  and and_9 (and_9_out, RegWrite, decoder_1_out8);
  and and_10 (and_10_out, RegWrite, decoder_1_out9);
  and and_11 (and_11_out, RegWrite, decoder_1_out10);
  and and_12 (and_12_out, RegWrite, decoder_1_out11);
  and and_13 (and_13_out, RegWrite, decoder_1_out12);
  and and_14 (and_14_out, RegWrite, decoder_1_out13);
  and and_15 (and_15_out, RegWrite, decoder_1_out14);
  and and_16 (and_16_out, RegWrite, decoder_1_out15);
  Register #(.width(16)) register_1 (.D(Write_Data_IN), .en(and_1_out), .Q(register_1_q), .clk(Clock));  // open: clr
  Register #(.width(16)) register_2 (.D(Write_Data_IN), .en(and_2_out), .Q(register_2_q), .clk(Clock));  // open: clr
  Register #(.width(16)) register_3 (.D(Write_Data_IN), .en(and_3_out), .Q(register_3_q), .clk(Clock));  // open: clr
  Register #(.width(16)) register_4 (.D(Write_Data_IN), .en(and_4_out), .Q(register_4_q), .clk(Clock));  // open: clr
  Register #(.width(16)) register_5 (.D(Write_Data_IN), .en(and_5_out), .Q(register_5_q), .clk(Clock));  // open: clr
  Register #(.width(16)) register_6 (.D(Write_Data_IN), .en(and_6_out), .Q(register_6_q), .clk(Clock));  // open: clr
  Register #(.width(16)) register_7 (.D(Write_Data_IN), .en(and_7_out), .Q(register_7_q), .clk(Clock));  // open: clr
  Register #(.width(16)) register_8 (.D(Write_Data_IN), .en(and_8_out), .Q(register_8_q), .clk(Clock));  // open: clr
  Register #(.width(16)) register_9 (.D(Write_Data_IN), .en(and_9_out), .Q(register_9_q), .clk(Clock));  // open: clr
  Register #(.width(16)) register_10 (.D(Write_Data_IN), .en(and_10_out), .Q(register_10_q), .clk(Clock));  // open: clr
  Register #(.width(16)) register_11 (.D(Write_Data_IN), .en(and_11_out), .Q(register_11_q), .clk(Clock));  // open: clr
  Register #(.width(16)) register_12 (.D(Write_Data_IN), .en(and_12_out), .Q(register_12_q), .clk(Clock));  // open: clr
  Register #(.width(16)) register_13 (.D(Write_Data_IN), .en(and_13_out), .Q(register_13_q), .clk(Clock));  // open: clr
  Register #(.width(16)) register_14 (.D(Write_Data_IN), .en(and_14_out), .Q(register_14_q), .clk(Clock));  // open: clr
  Register #(.width(16)) register_15 (.D(Write_Data_IN), .en(and_15_out), .Q(register_15_q), .clk(Clock));  // open: clr
  Register #(.width(16)) register_16 (.D(Write_Data_IN), .en(and_16_out), .Q(register_16_q), .clk(Clock));  // open: clr
  Multiplexer #(.select(4), .width(16)) multiplexer_1 (
    .in0(register_1_q), .in1(register_2_q), .in2(register_3_q), .in3(register_4_q), .in4(register_5_q),
    .in5(register_6_q), .in6(register_7_q), .in7(register_8_q), .in8(register_9_q), .in9(register_10_q),
    .in10(register_11_q), .in11(register_12_q), .in12(register_13_q), .in13(register_14_q),
    .in14(register_15_q), .in15(register_16_q), .out(Data01), .sel(RS));  // open: en
  Multiplexer #(.select(4), .width(16)) multiplexer_2 (
    .in0(register_1_q), .in1(register_2_q), .in2(register_3_q), .in3(register_4_q), .in4(register_5_q),
    .in5(register_6_q), .in6(register_7_q), .in7(register_8_q), .in8(register_9_q), .in9(register_10_q),
    .in10(register_11_q), .in11(register_12_q), .in12(register_13_q), .in13(register_14_q),
    .in14(register_15_q), .in15(register_16_q), .out(Data02), .sel(RT));  // open: en

  // Notes on the sheet:
  //   AbdullahMahmood
  //   Register Files
endmodule

module ALU_16_bit (
  input  Cin,
  input  B_Invert,
  input  A_Invert,
  input  [1:0] Operation_Code,
  input  [15:0] Input_B,
  input  [15:0] Input_A,
  output [15:0] Result,
  output Zero_Flag,
  output OverFlow
);

  wire alu_1_bit_1_cout, alu_1_bit_2_cout, alu_1_bit_3_cout, alu_1_bit_4_cout, alu_1_bit_5_cout,
       alu_1_bit_6_cout, alu_1_bit_7_cout, alu_1_bit_8_cout, alu_1_bit_9_cout, alu_1_bit_10_cout,
       alu_1_bit_11_cout, alu_1_bit_12_cout, alu_1_bit_13_cout, alu_1_bit_14_cout, alu_1_bit_15_cout,
       alu_1_bit_16_cout;

  ALU_1_bit alu_1_bit_1 (
    .A(Input_A[0]), .B(Input_B[0]), .Cout(alu_1_bit_1_cout), .Cin(Cin), .A_Invert(A_Invert),
    .B_Invert(B_Invert), .Select_Bit_Operation(Operation_Code), .Result(Result[0]));
  ALU_1_bit alu_1_bit_2 (
    .A(Input_A[1]), .B(Input_B[1]), .Cout(alu_1_bit_2_cout), .Cin(alu_1_bit_1_cout), .A_Invert(A_Invert),
    .B_Invert(B_Invert), .Select_Bit_Operation(Operation_Code), .Result(Result[1]));
  ALU_1_bit alu_1_bit_3 (
    .A(Input_A[2]), .B(Input_B[2]), .Cout(alu_1_bit_3_cout), .Cin(alu_1_bit_2_cout), .A_Invert(A_Invert),
    .B_Invert(B_Invert), .Select_Bit_Operation(Operation_Code), .Result(Result[2]));
  ALU_1_bit alu_1_bit_4 (
    .A(Input_A[3]), .B(Input_B[3]), .Cout(alu_1_bit_4_cout), .Cin(alu_1_bit_3_cout), .A_Invert(A_Invert),
    .B_Invert(B_Invert), .Select_Bit_Operation(Operation_Code), .Result(Result[3]));
  ALU_1_bit alu_1_bit_5 (
    .A(Input_A[4]), .B(Input_B[4]), .Cout(alu_1_bit_5_cout), .Cin(alu_1_bit_4_cout), .A_Invert(A_Invert),
    .B_Invert(B_Invert), .Select_Bit_Operation(Operation_Code), .Result(Result[4]));
  ALU_1_bit alu_1_bit_6 (
    .A(Input_A[5]), .B(Input_B[5]), .Cout(alu_1_bit_6_cout), .Cin(alu_1_bit_5_cout), .A_Invert(A_Invert),
    .B_Invert(B_Invert), .Select_Bit_Operation(Operation_Code), .Result(Result[5]));
  ALU_1_bit alu_1_bit_7 (
    .A(Input_A[6]), .B(Input_B[6]), .Cout(alu_1_bit_7_cout), .Cin(alu_1_bit_6_cout), .A_Invert(A_Invert),
    .B_Invert(B_Invert), .Select_Bit_Operation(Operation_Code), .Result(Result[6]));
  ALU_1_bit alu_1_bit_8 (
    .A(Input_A[7]), .B(Input_B[7]), .Cout(alu_1_bit_8_cout), .Cin(alu_1_bit_7_cout), .A_Invert(A_Invert),
    .B_Invert(B_Invert), .Select_Bit_Operation(Operation_Code), .Result(Result[7]));
  ALU_1_bit alu_1_bit_9 (
    .A(Input_A[8]), .B(Input_B[8]), .Cout(alu_1_bit_9_cout), .Cin(alu_1_bit_8_cout), .A_Invert(A_Invert),
    .B_Invert(B_Invert), .Select_Bit_Operation(Operation_Code), .Result(Result[8]));
  ALU_1_bit alu_1_bit_10 (
    .A(Input_A[9]), .B(Input_B[9]), .Cout(alu_1_bit_10_cout), .Cin(alu_1_bit_9_cout), .A_Invert(A_Invert),
    .B_Invert(B_Invert), .Select_Bit_Operation(Operation_Code), .Result(Result[9]));
  ALU_1_bit alu_1_bit_11 (
    .A(Input_A[10]), .B(Input_B[10]), .Cout(alu_1_bit_11_cout), .Cin(alu_1_bit_10_cout), .A_Invert(A_Invert),
    .B_Invert(B_Invert), .Select_Bit_Operation(Operation_Code), .Result(Result[10]));
  ALU_1_bit alu_1_bit_12 (
    .A(Input_A[11]), .B(Input_B[11]), .Cout(alu_1_bit_12_cout), .Cin(alu_1_bit_11_cout), .A_Invert(A_Invert),
    .B_Invert(B_Invert), .Select_Bit_Operation(Operation_Code), .Result(Result[11]));
  ALU_1_bit alu_1_bit_13 (
    .A(Input_A[12]), .B(Input_B[12]), .Cout(alu_1_bit_13_cout), .Cin(alu_1_bit_12_cout), .A_Invert(A_Invert),
    .B_Invert(B_Invert), .Select_Bit_Operation(Operation_Code), .Result(Result[12]));
  ALU_1_bit alu_1_bit_14 (
    .A(Input_A[13]), .B(Input_B[13]), .Cout(alu_1_bit_14_cout), .Cin(alu_1_bit_13_cout), .A_Invert(A_Invert),
    .B_Invert(B_Invert), .Select_Bit_Operation(Operation_Code), .Result(Result[13]));
  ALU_1_bit alu_1_bit_15 (
    .A(Input_A[14]), .B(Input_B[14]), .Cout(alu_1_bit_15_cout), .Cin(alu_1_bit_14_cout), .A_Invert(A_Invert),
    .B_Invert(B_Invert), .Select_Bit_Operation(Operation_Code), .Result(Result[14]));
  ALU_1_bit alu_1_bit_16 (
    .A(Input_A[15]), .B(Input_B[15]), .Cout(alu_1_bit_16_cout), .Cin(alu_1_bit_15_cout), .A_Invert(A_Invert),
    .B_Invert(B_Invert), .Select_Bit_Operation(Operation_Code), .Result(Result[15]));
  nor nor_1 (Zero_Flag, Result[0], Result[1], Result[2], Result[3], Result[4], Result[5], Result[6], Result[7], Result[8], Result[9], Result[10], Result[11], Result[12], Result[13], Result[14], Result[15]);
  xor xor_1 (OverFlow, alu_1_bit_15_cout, alu_1_bit_16_cout);

  // Notes on the sheet:
  //   AbdullahMahmood
  //   ALU 16 BIT
endmodule

// 1 Bit ALU
module ALU_1_bit (
  input  Cin,
  input  A,
  input  A_Invert,
  input  B,
  input  B_Invert,
  input  [1:0] Select_Bit_Operation,
  output Result,
  output Cout
);

  wire adder_1_out, AND_out, multiplexer_1_out, multiplexer_2_out, not_1_out, not_2_out, OR_out, xor_out;

  Multiplexer multiplexer_1 (.in0(A), .in1(not_1_out), .out(multiplexer_1_out), .sel(A_Invert));  // open: en
  not not_1 (not_1_out, A);
  not not_2 (not_2_out, B);
  Multiplexer multiplexer_2 (.in0(B), .in1(not_2_out), .out(multiplexer_2_out), .sel(B_Invert));  // open: en
  and AND (AND_out, multiplexer_1_out, multiplexer_2_out);
  or OR (OR_out, multiplexer_1_out, multiplexer_2_out);
  xor \xor  (xor_out, multiplexer_1_out, multiplexer_2_out);
  Adder #(.width(1)) adder_1 (.a(multiplexer_1_out), .b(multiplexer_2_out), .out(adder_1_out), .cin(Cin), .cout(Cout));
  Multiplexer #(.select(2)) multiplexer_3 (
    .in0(AND_out), .in1(OR_out), .in2(xor_out), .in3(adder_1_out), .out(Result), .sel(Select_Bit_Operation));  // open: en

  // Notes on the sheet:
  //   AbdullahMahmood
  //   ALU 1BIT
endmodule

module BranchCircuit (
  input  Beq_Bne_CU_Line_In,
  input  Branch_CU_Line_In,
  input  ALU_Zero_Flag_IN,
  output Output_to_MUX
);

  wire not_1_out, xor_1_out;

  and and_1 (Output_to_MUX, Beq_Bne_CU_Line_In, not_1_out);
  not not_1 (not_1_out, xor_1_out);
  xor xor_1 (xor_1_out, Branch_CU_Line_In, ALU_Zero_Flag_IN);

  // Notes on the sheet:
  //   Branch Circuit
  //   Instructions    Branch    ALUZ    BCU   Output    invert
  //   BNE                    0             0        1         1            0
  //   BNE                    0             1        1         0            1
  //   BEQ                    1             0        1         0            1
  //   BEQ                    1             1        1         1            0
  //   Other ins             0             0        0         0
  //   Other ins             0             1        0         0
  //   Truth Table 
  //   AND Gate
  //   Xor + Not Gate
  //   AbdullahMahmood
endmodule

module MainControlUnit_V1 (
  input  [3:0] Ins_Input,
  output RegWrite,
  output ALUsrc,
  output Binvert,
  output A_invert,
  output MemToReg,
  output MemRead,
  output MemWrite,
  output Branch,
  output REGDst,
  output [1:0] ALUop,
  output BEQ_BNE_Line
);

  wire ADD_0000_out, ADDi_1000_out, AND_0100_out, ANDi_1100_out, BNE_1111_out, NAND_0110_out, Nor_0010_out,
       OR_0011_out, ORi_1011_out, Sub_0001_out, SUBi_0111_out, XOR_0101_out, XORi_1101_out;

  and ADD_0000 (ADD_0000_out, ~Ins_Input[3], ~Ins_Input[2], ~Ins_Input[1], ~Ins_Input[0]);  // AND_Gate
  and Sub_0001 (Sub_0001_out, ~Ins_Input[3], ~Ins_Input[2], ~Ins_Input[1], Ins_Input[0]);  // AND_Gate
  and Nor_0010 (Nor_0010_out, ~Ins_Input[3], ~Ins_Input[2], Ins_Input[1], ~Ins_Input[0]);  // AND_Gate
  and OR_0011 (OR_0011_out, ~Ins_Input[3], ~Ins_Input[2], Ins_Input[1], Ins_Input[0]);  // AND_Gate
  and AND_0100 (AND_0100_out, ~Ins_Input[3], Ins_Input[2], ~Ins_Input[1], ~Ins_Input[0]);  // AND_Gate
  and XOR_0101 (XOR_0101_out, ~Ins_Input[3], Ins_Input[2], ~Ins_Input[1], Ins_Input[0]);  // AND_Gate
  and NAND_0110 (NAND_0110_out, ~Ins_Input[3], Ins_Input[2], Ins_Input[1], ~Ins_Input[0]);  // AND_Gate
  and SUBi_0111 (SUBi_0111_out, ~Ins_Input[3], Ins_Input[2], Ins_Input[1], Ins_Input[0]);  // AND_Gate
  and ADDi_1000 (ADDi_1000_out, Ins_Input[3], ~Ins_Input[2], ~Ins_Input[1], ~Ins_Input[0]);  // AND_Gate
  and lw_1001 (MemRead, Ins_Input[3], ~Ins_Input[2], ~Ins_Input[1], Ins_Input[0]);  // AND_Gate
  and sw_1010 (MemWrite, Ins_Input[3], ~Ins_Input[2], Ins_Input[1], ~Ins_Input[0]);  // AND_Gate
  and ORi_1011 (ORi_1011_out, Ins_Input[3], ~Ins_Input[2], Ins_Input[1], Ins_Input[0]);  // AND_Gate
  and ANDi_1100 (ANDi_1100_out, Ins_Input[3], Ins_Input[2], ~Ins_Input[1], ~Ins_Input[0]);  // AND_Gate
  and XORi_1101 (XORi_1101_out, Ins_Input[3], Ins_Input[2], ~Ins_Input[1], Ins_Input[0]);  // AND_Gate
  and BEQ_1110 (Branch, Ins_Input[3], Ins_Input[2], Ins_Input[1], ~Ins_Input[0]);  // AND_Gate
  and BNE_1111 (BNE_1111_out, Ins_Input[3], Ins_Input[2], Ins_Input[1], Ins_Input[0]);
  or or_1 (RegWrite, ADD_0000_out, Sub_0001_out, Nor_0010_out, OR_0011_out, AND_0100_out, XOR_0101_out, NAND_0110_out, SUBi_0111_out, ADDi_1000_out, MemRead, ORi_1011_out, ANDi_1100_out, XORi_1101_out);
  or or_2 (ALUsrc, SUBi_0111_out, ADDi_1000_out, MemRead, MemWrite, ORi_1011_out, ANDi_1100_out, XORi_1101_out);
  or or_3 (Binvert, NAND_0110_out, Sub_0001_out, Nor_0010_out, SUBi_0111_out, Branch, BNE_1111_out);
  or or_4 (A_invert, NAND_0110_out, Nor_0010_out);
  or or_5 (REGDst, Branch, MemWrite, BNE_1111_out);
  or _1st (ALUop[1], ADD_0000_out, Sub_0001_out, XOR_0101_out, SUBi_0111_out, ADDi_1000_out, MemRead, MemWrite, XORi_1101_out, Branch, BNE_1111_out);
  or _2nd (ALUop[0], ADD_0000_out, Sub_0001_out, OR_0011_out, SUBi_0111_out, ADDi_1000_out, NAND_0110_out, MemRead, MemWrite, ORi_1011_out, Branch, BNE_1111_out);
  or or_6 (BEQ_BNE_Line, BNE_1111_out, Branch);

  assign MemToReg = MemRead;

  // Notes on the sheet:
  //   AbdullahMahmood
  //   0     1     2      3     4       5      6      7      8     9     10     11    12    13     14    15  
  //   Main Control Unit V1
endmodule

module MainControlUnit_Kmap_V2 (
  input  [3:0] Ins_Input,
  output A_Invert,
  output B_Invert,
  output RegWrite,
  output ALUSrc,
  output REGdst,
  output MemToReg,
  output MemRead,
  output MemWrite,
  output Branch,
  output BEQ___BNE_Line,
  output [1:0] ALUOp
);

  wire and_1_out, and_2_out, and_3_out, and_4_out, and_5_out, and_6_out, and_7_out, and_8_out, and_9_out,
       and_10_out, and_11_out, and_12_out, and_13_out, and_14_out, and_15_out, and_16_out, not_1_out,
       not_2_out, not_3_out, not_4_out, not_5_out, not_6_out, not_7_out, not_8_out, not_9_out, not_10_out,
       not_11_out, not_12_out, not_13_out, not_14_out, not_15_out, not_16_out, not_17_out, not_18_out,
       not_19_out, not_20_out, not_21_out, not_22_out, not_23_out, not_24_out, not_25_out, not_26_out;

  not not_1 (not_1_out, Ins_Input[3]);
  not not_2 (not_2_out, Ins_Input[2]);
  not not_3 (not_3_out, Ins_Input[1]);
  not not_4 (not_4_out, Ins_Input[0]);
  not not_5 (not_5_out, Ins_Input[2]);
  not not_6 (not_6_out, Ins_Input[1]);
  not not_7 (not_7_out, Ins_Input[2]);
  not not_8 (not_8_out, Ins_Input[0]);
  not not_9 (not_9_out, Ins_Input[2]);
  not not_10 (not_10_out, Ins_Input[1]);
  not not_11 (not_11_out, Ins_Input[1]);
  not not_12 (not_12_out, Ins_Input[0]);
  not not_13 (not_13_out, Ins_Input[3]);
  not not_14 (not_14_out, Ins_Input[0]);
  not not_15 (not_15_out, Ins_Input[2]);
  and and_1 (and_1_out, Ins_Input[3], not_16_out);
  not not_16 (not_16_out, Ins_Input[2]);
  and and_2 (and_2_out, Ins_Input[3], not_17_out);
  not not_17 (not_17_out, Ins_Input[1]);
  and and_3 (and_3_out, Ins_Input[3], Ins_Input[1], not_4_out);
  and and_4 (and_4_out, Ins_Input[3], Ins_Input[2], Ins_Input[1]);
  and and_5 (and_5_out, not_5_out, not_6_out);
  and and_6 (and_6_out, not_7_out, Ins_Input[0]);
  and and_7 (and_7_out, Ins_Input[3], Ins_Input[1]);
  and and_8 (and_8_out, Ins_Input[2], Ins_Input[1], not_8_out);
  and and_9 (and_9_out, not_9_out, not_10_out);
  and and_10 (and_10_out, not_11_out, Ins_Input[0]);
  and and_11 (and_11_out, Ins_Input[3], Ins_Input[1], not_12_out);
  and and_12 (and_12_out, Ins_Input[3], Ins_Input[2], Ins_Input[0]);
  not not_18 (not_18_out, Ins_Input[3]);
  not not_19 (not_19_out, Ins_Input[0]);
  and and_13 (and_13_out, not_13_out, Ins_Input[1], not_14_out);
  and and_14 (and_14_out, Ins_Input[3], Ins_Input[2], Ins_Input[1]);
  and and_15 (and_15_out, not_1_out, not_2_out, not_3_out, Ins_Input[0]);
  not not_20 (not_20_out, Ins_Input[3]);
  not not_21 (not_21_out, Ins_Input[1]);
  and and_16 (and_16_out, not_15_out, Ins_Input[0]);
  not not_22 (not_22_out, Ins_Input[2]);
  not not_23 (not_23_out, Ins_Input[1]);
  not not_24 (not_24_out, Ins_Input[2]);
  not not_25 (not_25_out, Ins_Input[0]);
  not not_26 (not_26_out, Ins_Input[0]);
  and and_17 (A_Invert, not_18_out, Ins_Input[1], not_19_out);
  or or_1 (B_Invert, and_13_out, and_14_out, and_15_out);
  or or_2 (RegWrite, not_20_out, not_21_out, and_16_out);
  or or_3 (ALUSrc, and_1_out, and_2_out);
  or or_4 (REGdst, and_3_out, and_4_out);
  and and_18 (MemRead, Ins_Input[3], not_22_out, not_23_out, Ins_Input[0]);
  and and_19 (MemWrite, Ins_Input[3], not_24_out, Ins_Input[1], not_25_out);
  and and_20 (Branch, Ins_Input[3], Ins_Input[2], Ins_Input[1], not_26_out);
  and and_21 (BEQ___BNE_Line, Ins_Input[3], Ins_Input[2], Ins_Input[1]);
  or or_5 (ALUOp[0], and_5_out, and_6_out, and_7_out, and_8_out);
  or or_6 (ALUOp[1], and_9_out, and_10_out, and_11_out, and_12_out);

  assign MemToReg = MemRead;

  // Notes on the sheet:
  //   A B C D
  //   A B C D
  //   Main Control Unit Kmap V2
endmodule
